// Logisim project lab1.2.circ as structural Verilog: 1 circuit, main circuit cmos_or
module cmos_or (
  input  X,
  input  Y,
  output Z
);

  wire transistor_3_out;

  Transistor #(.\type ("n")) transistor_1 (.in(1'b1), .out(Z), .gate(X));
  Transistor transistor_2 (.in(transistor_3_out), .out(Z), .gate(Y));
  Transistor transistor_3 (.in(1'b0), .out(transistor_3_out), .gate(X));
  Transistor #(.\type ("n")) transistor_4 (.in(1'b1), .out(Z), .gate(Y));

  // Notes on the sheet:
  //   输入引脚
  //   请勿增加、删除引脚，用隧道标签构建电路
  //   请勿更改电路封装外观
  //   提示：使用三极管组件实现或门电路，禁止直接使用逻辑门组件。
  //   输出引脚
endmodule
