// Logisim project think.circ as structural Verilog: 3 circuits, main circuit n-and
module n_and (
  input  D0,
  input  D1,
  input  D2,
  input  D3,
  input  S0,
  input  S1,
  output Y
);

  wire nand_1_out, nand_2_out, nand_3_out, nand_4_out, nand_5_out, nand_6_out, nand_7_out, nand_8_out;

  nand nand_1 (nand_1_out, S1, S1);
  nand nand_2 (nand_2_out, S0, S0);
  nand nand_3 (nand_3_out, S0, S0);
  nand nand_4 (nand_4_out, S1, S1);
  nand nand_5 (nand_5_out, D3, S0, S1);
  nand nand_6 (nand_6_out, D2, S0, nand_1_out);
  nand nand_7 (nand_7_out, D1, nand_2_out, S1);
  nand nand_8 (nand_8_out, D0, nand_3_out, nand_4_out);
  nand nand_9 (Y, nand_5_out, nand_6_out, nand_7_out, nand_8_out);
endmodule

module grey (
  input  I0,
  input  I1,
  input  I2,
  input  I3,
  output O0,
  output O1,
  output O2,
  output O3
);

  xor xor_1 (O0, I0, I1);
  xor xor_2 (O1, I1, I2);
  xor xor_3 (O2, I2, I3);
  xor xor_4 (O3, I3, I0);
endmodule

module check (
  input  D0,
  input  D1,
  input  D2,
  input  D3,
  output Check
);

  wire xor_1_out, xor_2_out;

  xor xor_1 (xor_1_out, D0, D1);
  xor xor_2 (xor_2_out, D2, D3);
  xor xor_3 (Check, xor_1_out, xor_2_out);
endmodule
