// Logisim project lab2.2.circ as structural Verilog: 1 circuit, main circuit main
module main (
  input  I0,
  input  I1,
  input  I2,
  input  I4,
  input  I5,
  input  I3,
  input  I6,
  input  I7,
  output O0,
  output O1,
  output O2
);

  wire and_1_out, and_2_out, and_3_out, and_4_out, and_5_out, and_6_out, and_7_out;
  wire [3:3] not_1_out;

  and and_1 (and_1_out, ~I0, I1);  // AND_Gate
  and and_2 (and_2_out, ~I0, ~I1, I2);  // AND_Gate
  and and_3 (and_3_out, ~I0, ~I1, ~I2, I3);  // AND_Gate
  and and_4 (and_4_out, ~I0, ~I1, ~I2, ~I3, I4);  // AND_Gate
  and and_5 (and_5_out, ~I0, ~I1, ~I2, ~I3, ~I4, I5);  // AND_Gate
  and and_6 (and_6_out, ~I0, ~I1, ~I2, ~I3, ~I4, ~I5, I6);  // AND_Gate
  and and_7 (and_7_out, ~I0, ~I1, ~I2, ~I3, ~I4, ~I5, ~I6, I7);  // AND_Gate
  or or_1 (O0, and_5_out, and_4_out, and_6_out, and_7_out);
  or or_2 (O1, and_2_out, and_3_out, and_6_out, and_7_out);
  or or_3 (O2, and_7_out, and_5_out, and_3_out, and_1_out);
  not not_1 (not_1_out[3], 1'b1);
  Hex_Digit_Display hex_digit_display_1 (.value({not_1_out[3], O0, O1, O2}));  // open: dp

  // Notes on the sheet:
  //   输入引脚
  //   请勿修改引脚名称、电路名称及电路封装外观
  //   提示：使用独立逻辑门实现8-3优先级编码器，禁止直接使用编码器组件。
  //   输出引脚
endmodule
