// Logisim project lab2.4.circ as structural Verilog: 2 circuits, main circuit main
module main (
  input  [6:0] Input,
  output [6:0] Output,
  output NoError
);

  wire main_1_y0_l, main_1_y1_l, main_1_y2_l, main_1_y3_l, main_1_y4_l, main_1_y5_l, main_1_y6_l,
       main_1_y7_l, \n4位奇偶校验器_1_odd , \n4位奇偶校验器_2_odd , \n4位奇偶校验器_3_odd , not_2_out, not_3_out, not_4_out,
       not_5_out, not_6_out, not_7_out, not_8_out;

  \_4位奇偶校验器  \u_4位奇偶校验器_1  (
    .N0(Input[6]), .N1(Input[4]), .N2(Input[2]), .N3(Input[0]), .ODD(\n4位奇偶校验器_1_odd ));  // open: EVEN
  \_4位奇偶校验器  \u_4位奇偶校验器_2  (
    .N0(Input[6]), .N1(Input[5]), .N2(Input[2]), .N3(Input[1]), .ODD(\n4位奇偶校验器_2_odd ));  // open: EVEN
  \_4位奇偶校验器  \u_4位奇偶校验器_3  (
    .N0(Input[6]), .N1(Input[5]), .N2(Input[4]), .N3(Input[3]), .ODD(\n4位奇偶校验器_3_odd ));  // open: EVEN
  not not_1 (NoError, main_1_y0_l);
  lab2_1_main main_1 (
    .Y0_L(main_1_y0_l), .G1(1'b1), .G2A_L(1'b0), .G2B_L(1'b0), .A(\n4位奇偶校验器_1_odd ), .B(\n4位奇偶校验器_2_odd ),
    .C(\n4位奇偶校验器_3_odd ), .Y2_L(main_1_y2_l), .Y3_L(main_1_y3_l), .Y4_L(main_1_y4_l), .Y5_L(main_1_y5_l),
    .Y6_L(main_1_y6_l), .Y7_L(main_1_y7_l), .Y1_L(main_1_y1_l));
  not not_2 (not_2_out, main_1_y1_l);
  not not_3 (not_3_out, main_1_y2_l);
  not not_4 (not_4_out, main_1_y3_l);
  not not_5 (not_5_out, main_1_y4_l);
  not not_6 (not_6_out, main_1_y5_l);
  not not_7 (not_7_out, main_1_y6_l);
  not not_8 (not_8_out, main_1_y7_l);
  xor xor_1 (Output[0], Input[0], not_2_out);
  xor xor_2 (Output[1], Input[1], not_3_out);
  xor xor_3 (Output[2], Input[2], not_4_out);
  xor xor_4 (Output[3], Input[3], not_5_out);
  xor xor_5 (Output[4], Input[4], not_6_out);
  xor xor_6 (Output[5], Input[5], not_7_out);
  xor xor_7 (Output[6], Input[6], not_8_out);
  Hex_Digit_Display hex_digit_display_1 ();  // open: value, dp

  // Notes on the sheet:
  //   输入引脚
  //   输入引脚
  //   请勿修改引脚名称、电路名称及电路封装外观
  //   提示：使用异或门、4位奇偶校验电路和74x138子电路实现7位汉明码纠错电路。
  //   输出引脚
endmodule

module \_4位奇偶校验器  (
  input  N0,
  input  N1,
  input  N2,
  input  N3,
  output EVEN,
  output ODD
);

  xor xor_1 (ODD, N0, N1, N2, N3);
  not not_1 (EVEN, ODD);

  // Notes on the sheet:
  //   4位奇偶校验电路
endmodule
