// Logisim project think1&2.circ as structural Verilog: 2 circuits, main circuit main
module main (
  input  [3:0] X,
  input  [3:0] Y,
  input  Cin,
  output [3:0] F,
  output Cout
);

  wire CF_out, FA0_cout, FA1_cout, FA2_cout, OF_out, SF_out, xor_1_out, xor_2_out, xor_3_out, xor_4_out,
       ZF_out;

  Hex_Digit_Display hex_digit_display_1 (.value(X));  // open: dp
  Hex_Digit_Display hex_digit_display_2 (.value(Y));  // open: dp
  FA FA0 (.A(X[0]), .B(xor_1_out), .Cin(Cin), .Cout(FA0_cout), .F(F[0]));
  xor xor_1 (xor_1_out, Y[0], Cin);
  xor xor_2 (xor_2_out, Y[1], Cin);
  Hex_Digit_Display hex_digit_display_3 (.value(F));  // open: dp
  FA FA1 (.A(X[1]), .B(xor_2_out), .Cin(FA0_cout), .Cout(FA1_cout), .F(F[1]));
  xor xor_3 (xor_3_out, Y[2], Cin);
  FA FA2 (.A(X[2]), .B(xor_3_out), .Cin(FA1_cout), .Cout(FA2_cout), .F(F[2]));
  xor xor_4 (xor_4_out, Y[3], Cin);
  FA FA3 (.A(X[3]), .B(xor_4_out), .Cin(FA2_cout), .Cout(Cout), .F(F[3]));
  nor ZF (ZF_out, F[0], F[1], F[2], F[3]);
  buf SF (SF_out, F[3]);
  xor OF (OF_out, FA2_cout, Cout);
  xor CF (CF_out, Cout, Cin);

  // Other names for the same wires on the sheet: SUM[3:0] = F; 操作数x[3:0] = X; 操作数y[3:0] = Y

  // Notes on the sheet:
  //   输入引脚
  //   +
  //   =
  //   请勿修改引脚名称、电路名称及电路封装外观
  //   提示：使用独立逻辑门及全加器FA子电路实现4位二进制数加减法器，禁止直接使用加减法器组件。
  //   输出引脚
endmodule

module FA (
  input  A,
  input  B,
  input  Cin,
  output F,
  output Cout
);

  wire and_1_out, and_2_out, and_3_out;

  xor xor_1 (F, A, B, Cin);
  and and_1 (and_1_out, A, B);
  and and_2 (and_2_out, B, Cin);
  or or_1 (Cout, and_1_out, and_2_out, and_3_out);
  and and_3 (and_3_out, A, Cin);

  // Notes on the sheet:
  //   全加器
endmodule
