// Logisim project lab2.5.circ as structural Verilog: 1 circuit, main circuit main
module main (
  input  [7:0] DataIn,
  input  [2:0] shamt,
  input  L_R,
  input  A_L,
  input  IN,
  output [7:0] DataOut
);

  wire [0:0] multiplexer_2_out;
  wire [1:0] multiplexer_3_out_2, multiplexer_4_out;
  wire [3:0] multiplexer_6_out;
  wire [5:0] multiplexer_3_out;
  wire [7:0] multiplexer_5_out;
  wire [7:7] multiplexer_1_out;

  Multiplexer #(.enable("false")) multiplexer_1 (.in0(IN), .in1(DataIn[7]), .out(multiplexer_1_out[7]), .sel(A_L));
  Multiplexer #(.enable("false")) multiplexer_2 (.in0(IN), .in1(DataIn[7]), .out(multiplexer_2_out[0]), .sel(A_L));
  Multiplexer #(.select(2), .width(8), .enable("false")) multiplexer_3 (
    .in0(DataIn), .in1({multiplexer_1_out[7], DataIn[7:1]}), .in2(DataIn),
    .in3({DataIn[6:0], multiplexer_2_out[0]}),
    .out({multiplexer_3_out_2[0], multiplexer_3_out_2[1], multiplexer_3_out}), .sel({L_R, shamt[0]}));
  Multiplexer #(.width(2), .enable("false")) multiplexer_4 (
    .in0({2{IN}}), .in1(multiplexer_3_out_2), .out(multiplexer_4_out), .sel(A_L));
  Multiplexer #(.select(2), .width(8), .enable("false")) multiplexer_5 (
    .in0({multiplexer_3_out_2[0], multiplexer_3_out_2[1], multiplexer_3_out}),
    .in1({{2{multiplexer_1_out[7]}}, multiplexer_3_out_2[0], multiplexer_3_out_2[1], multiplexer_3_out[5:2]}),
    .in2({multiplexer_3_out_2[0], multiplexer_3_out_2[1], multiplexer_3_out}),
    .in3({multiplexer_3_out, multiplexer_4_out[0], multiplexer_4_out[1]}), .out(multiplexer_5_out),
    .sel({L_R, shamt[1]}));
  Multiplexer #(.width(4), .enable("false")) multiplexer_6 (
    .in0({4{IN}}),
    .in1({multiplexer_5_out[4], multiplexer_5_out[5], multiplexer_5_out[6], multiplexer_5_out[7]}),
    .out(multiplexer_6_out), .sel(A_L));
  Multiplexer #(.select(2), .width(8), .enable("false")) multiplexer_7 (
    .in0(multiplexer_5_out), .in1({{4{multiplexer_1_out[7]}}, multiplexer_5_out[7:4]}),
    .in2(multiplexer_5_out),
    .in3({multiplexer_5_out[3:0], multiplexer_6_out[0], multiplexer_6_out[1], multiplexer_6_out[2], multiplexer_6_out[3]}),
    .out(DataOut), .sel({L_R, shamt[2]}));

  // Other names for the same wires on the sheet: Din[7:0] = DataIn; Input = IN; Left_Right = L_R; Arth_Logic = A_L;
  //   Dout[7:0] = DataOut

  // Notes on the sheet:
  //   L/R,A/L: 00逻辑右移，01算术右移，10逻辑左移，11：循环左移
  //   输入引脚
  //   请勿修改引脚名称、电路名称及电路封装外观
  //   提示：使用多路选择器级联实现8位桶形移位器，禁止直接使用移位器组件。
  //   输出引脚
endmodule
