// Logisim project lab4 16mul.circ as structural Verilog: 1 circuit, main circuit main
module main (
  input  in_1,
  input  in_2,
  input  [15:0] in_3,
  input  [15:0] in_4,
  output [31:0] out_5
);

  wire LOAD, not_1_out, STOP;
  wire [4:0] cntr4u_1_q0;
  wire [15:0] adder_1_out, multiplexer_1_out, multiplexer_2_out;
  wire [15:15] adder_1_cout;

  Multiplexer #(.width(16), .enable("false")) multiplexer_1 (
    .in0({16{1'b0}}), .in1(in_3), .out(multiplexer_1_out), .sel(out_5[0]));
  not not_1 (not_1_out, STOP);
  Adder #(.width(16)) adder_1 (
    .a(multiplexer_1_out), .b(out_5[31:16]), .out(adder_1_out), .cin(1'b0), .cout(adder_1_cout[15]));
  Register #(.width(16), .Select("low")) P (
    .D({adder_1_cout[15], adder_1_out[15:1]}), .en(not_1_out), .Q(out_5[31:16]), .clk(in_1), .clr(in_2));
  Register #(.width(16), .Select("low")) Y (
    .D(multiplexer_2_out), .en(not_1_out), .Q(out_5[15:0]), .clk(in_1), .clr(in_2));
  Multiplexer #(.width(16), .enable("false")) multiplexer_2 (
    .in0({adder_1_out[0], out_5[15:1]}), .in1(in_4), .out(multiplexer_2_out), .sel(LOAD));
  CNTR4U cntr4u_1 (
    .CLK(in_1), .LD(in_2), .CLR(in_2), .Q0(cntr4u_1_q0[0]), .Q1(cntr4u_1_q0[1]), .D0(1'b0), .D1(1'b0),
    .D2(1'b0), .Q2(cntr4u_1_q0[2]), .Q3(cntr4u_1_q0[3]), .D3(1'b0), .ENP(1'b1), .ENT(1'b1), .D4(1'b0),
    .Q4(cntr4u_1_q0[4]));  // open: RCO, D5, Q5
  Comparator #(.width(5), .mode("unsigned")) comparator_1 (.a(cntr4u_1_q0), .b({5{1'b0}}), .eq(LOAD));  // open: gt, lt
  Comparator #(.width(5), .mode("unsigned")) comparator_2 (.a(cntr4u_1_q0), .b(5'b10001), .eq(STOP));  // open: gt, lt

  // Other names for the same wires on the sheet: CLK = in_1; RST = in_2; X[15:0] = in_3; Y[15:0] = in_4;
  //   Z[31:0] = out_5
endmodule
