// Logisim project lab4 div.circ as structural Verilog: 1 circuit, main circuit main
module main (
  input  [31:0] in_1,
  input  in_2,
  input  [31:0] in_3,
  output [31:0] out_4,
  output [31:0] out_5
);

  wire CLK, comparator_1_gt, LOAD, not_1_out, not_2_out, START, STOP;
  wire [0:0] multiplexer_5_out;
  wire [5:0] cntr4u_1_q0;
  wire [31:0] multiplexer_1_out, multiplexer_2_out, multiplexer_3_out, multiplexer_4_out, subtractor_1_out;

  Clock clock_1 (.out(CLK));
  not not_1 (not_1_out, STOP);
  Multiplexer #(.width(32), .enable("false")) multiplexer_1 (
    .in0(multiplexer_4_out), .in1({32{1'b0}}), .out(multiplexer_1_out), .sel(LOAD));
  Register #(.width(32), .Select("low")) R1 (.D(multiplexer_1_out), .en(not_1_out), .Q(out_5), .clk(CLK), .clr(in_2));
  Subtractor #(.width(32)) subtractor_1 (.a(multiplexer_3_out), .b(in_3), .out(subtractor_1_out));  // open: bin, bout
  Multiplexer #(.width(32), .enable("false")) multiplexer_2 (
    .in0({out_4[30:0], multiplexer_5_out[0]}), .in1(in_1), .out(multiplexer_2_out), .sel(LOAD));
  Register #(.width(32), .Select("low")) Q (.D(multiplexer_2_out), .en(not_1_out), .Q(out_4), .clk(CLK), .clr(in_2));
  Multiplexer #(.width(32), .enable("false")) multiplexer_3 (
    .in0({out_5[30:0], out_4[31]}), .in1(out_5), .out(multiplexer_3_out), .sel(START));
  Multiplexer #(.width(32), .enable("false")) multiplexer_4 (
    .in0(multiplexer_3_out), .in1(subtractor_1_out), .out(multiplexer_4_out), .sel(multiplexer_5_out[0]));
  Multiplexer #(.enable("false")) multiplexer_5 (
    .in0(1'b0), .in1(1'b1), .out(multiplexer_5_out[0]), .sel(comparator_1_gt));
  Comparator #(.width(32)) comparator_1 (.a(subtractor_1_out), .b({32{1'b0}}), .gt(comparator_1_gt));  // open: eq, lt
  not not_2 (not_2_out, STOP);
  CNTR4U cntr4u_1 (
    .CLK(CLK), .LD(in_2), .CLR(in_2), .Q0(cntr4u_1_q0[0]), .Q1(cntr4u_1_q0[1]), .Q2(cntr4u_1_q0[2]),
    .Q3(cntr4u_1_q0[3]), .ENP(not_2_out), .ENT(not_2_out), .Q4(cntr4u_1_q0[4]), .Q5(cntr4u_1_q0[5]));  // open: D0, D1, D2, D3, RCO, D4, D5
  Comparator #(.width(6), .mode("unsigned")) comparator_2 (.a(cntr4u_1_q0), .b({6{1'b0}}), .eq(LOAD));  // open: gt, lt
  Comparator #(.width(6), .mode("unsigned")) comparator_3 (.a(cntr4u_1_q0), .b(6'b100001), .eq(STOP));  // open: gt, lt
  Comparator #(.width(6), .mode("unsigned")) comparator_4 (.a(cntr4u_1_q0), .b(6'b000001), .eq(START));  // open: gt, lt

  // Other names for the same wires on the sheet: 余数[31:0] = out_5; RST = in_2; X[31:0] = in_1; Y[31:0] = in_3;
  //   商[31:0] = out_4
endmodule
