// Logisim project lab4.5.circ as structural Verilog: 2 circuits, main circuit ALU
module ALU (
  input  [3:0] ALUctr,
  input  [31:0] A,
  input  [31:0] B,
  input  in_4,
  input  in_5,
  output Zero,
  output [31:0] S
);

  wire aluctrl_1_alctr, aluctrl_1_sftctr, aluctrl_1_sigctr, aluctrl_1_subctr, main_2_cf, main_2_of,
       main_2_sf, multiplexer_1_out, xor_3_out;
  wire [2:0] aluctrl_1_opctr;
  wire [31:0] and_1_out, bit_extender_1_out, bit_extender_2_out, main_1_dataout, main_2_s, main_3_out_5,
       or_1_out, xor_1_out, xor_2_out;

  assign bit_extender_1_out = {{31{aluctrl_1_subctr}}, aluctrl_1_subctr};  // Bit_Extender bit_extender_1
  assign xor_1_out = bit_extender_1_out ^ B;  // XOR_Gate xor_1, 32 bits wide
  assign and_1_out = A & B;  // AND_Gate and_1, 32 bits wide
  assign or_1_out = A | B;  // OR_Gate or_1, 32 bits wide
  assign xor_2_out = A ^ B;  // XOR_Gate xor_2, 32 bits wide
  lab4_4_main main_1 (
    .L_R(aluctrl_1_sftctr), .shamt(B[4:0]), .DataIn(A), .DataOut(main_1_dataout), .A_L(aluctrl_1_alctr));
  lab4_3_main main_2 (
    .Cin(aluctrl_1_subctr), .X(A), .Y(xor_1_out), .S(main_2_s), .OF(main_2_of), .CF(main_2_cf), .ZF(Zero),
    .SF(main_2_sf));  // open: Cout
  ALUctrl aluctrl_1 (
    .ALUctr(ALUctr), .SUBctr(aluctrl_1_subctr), .SFTctr(aluctrl_1_sftctr), .SIGctr(aluctrl_1_sigctr),
    .ALctr(aluctrl_1_alctr), .OPctr(aluctrl_1_opctr));
  xor xor_3 (xor_3_out, main_2_of, main_2_sf);
  lab4_16mul_main main_3 (.out_5(main_3_out_5), .in_1(in_4), .in_2(in_5), .in_3(B[15:0]), .in_4(A[15:0]));
  Multiplexer #(.enable("false")) multiplexer_1 (
    .in0(main_2_cf), .in1(xor_3_out), .out(multiplexer_1_out), .sel(aluctrl_1_sigctr));
  Multiplexer #(.select(3), .width(32), .enable("false")) multiplexer_2 (
    .in0(main_2_s), .in1(and_1_out), .in2(or_1_out), .in3(xor_2_out), .in4(main_1_dataout), .in5(B),
    .in6(bit_extender_2_out), .in7(main_3_out_5), .out(S), .sel(aluctrl_1_opctr));
  // Probe on A
  // Probe on B
  // Probe on S
  assign bit_extender_2_out = {{31{1'b0}}, multiplexer_1_out};  // Bit_Extender bit_extender_2

  // Other names for the same wires on the sheet: CLK = in_4; Result[31:0] = S; RST = in_5

  // Notes on the sheet:
  //   B: pull=down
  //   ALUctr: pull=down
  //   A: pull=down
  //   输入引脚
  //   请勿修改引脚名称、电路名称及电路封装外观
  //   提示：使用32位并行加法器子电路、桶形移位器、ALU控制子电路实现32位ALU
  //   功能说明:32位ALU，输入32位操作数A、B，4位控制信号ALUctr，输出32位结果Reseult和1位Zero标志位
  //   输出引脚
  //   操作数和结果
endmodule

// ALU操作控制信号
module ALUctrl (
  input  [3:0] ALUctr,
  output SUBctr,
  output SFTctr,
  output SIGctr,
  output ALctr,
  output [2:0] OPctr
);

  wire and_1_out, and_2_out, and_6_out, and_7_out, and_8_out, and_9_out, and_10_out, and_11_out, and_12_out,
       and_13_out, and_14_out, and_15_out;

  and and_1 (and_1_out, ~ALUctr[3], ~ALUctr[2], ALUctr[1]);  // AND_Gate
  and and_2 (and_2_out, ALUctr[3], ~ALUctr[2], ~ALUctr[1], ~ALUctr[0]);  // AND_Gate
  or or_1 (SUBctr, and_1_out, and_2_out);
  and and_3 (SIGctr, ~ALUctr[3], ~ALUctr[2], ALUctr[1], ~ALUctr[0]);  // AND_Gate
  and and_4 (ALctr, ALUctr[3], ALUctr[2], ~ALUctr[1], ALUctr[0]);  // AND_Gate
  and and_5 (SFTctr, ~ALUctr[3], ~ALUctr[2], ~ALUctr[1], ALUctr[0]);  // AND_Gate
  and and_6 (and_6_out, ~ALUctr[3], ~ALUctr[2], ALUctr[1]);  // AND_Gate
  and and_7 (and_7_out, ~ALUctr[3], ~ALUctr[1], ALUctr[0]);  // AND_Gate
  and and_8 (and_8_out, ALUctr[3], ALUctr[2], ALUctr[0]);
  and and_9 (and_9_out, ALUctr[3], ALUctr[2], ALUctr[1], ~ALUctr[0]);  // AND_Gate
  and and_10 (and_10_out, ~ALUctr[3], ~ALUctr[2], ALUctr[1]);  // AND_Gate
  and and_11 (and_11_out, ~ALUctr[3], ALUctr[2], ~ALUctr[0]);  // AND_Gate
  and and_12 (and_12_out, ALUctr[3], ALUctr[2], ALUctr[1], ~ALUctr[0]);  // AND_Gate
  and and_13 (and_13_out, ALUctr[3], ALUctr[2], ALUctr[1], ~ALUctr[0]);  // AND_Gate
  and and_14 (and_14_out, ~ALUctr[3], ALUctr[2], ~ALUctr[1], ~ALUctr[0]);  // AND_Gate
  and and_15 (and_15_out, ALUctr[2], ALUctr[1], ALUctr[0]);
  or or_2 (OPctr[2], and_6_out, and_7_out, and_8_out, and_9_out);
  or or_3 (OPctr[1], and_10_out, and_11_out, and_12_out);
  or or_4 (OPctr[0], and_13_out, and_14_out, and_15_out);

  // Other names for the same wires on the sheet: LRctr = SFTctr

  // Notes on the sheet:
  //   输入引脚
  //   ALU操作控制信号生成部件
  //   输出引脚
endmodule
