// Logisim project lab5 think light.circ as structural Verilog: 2 circuits, main circuit main
// ASCII-ZK
module main (
  input  [6:0] ASCII_CODE,
  output [7:0] row1,
  output [7:0] row2,
  output [7:0] row3,
  output [7:0] row4,
  output [7:0] row5,
  output [7:0] row6,
  output [7:0] row7,
  output [7:0] row8,
  output [7:0] row9,
  output [7:0] row10,
  output [7:0] row11,
  output [7:0] row12,
  output [7:0] row13,
  output [7:0] row14,
  output [7:0] row15,
  output [7:0] row16
);

  wire [6:0] subtractor_1_out;
  wire [10:0] adder_1_out, adder_2_out, adder_3_out, adder_4_out, adder_5_out, adder_6_out, adder_7_out,
       adder_8_out, adder_9_out, adder_10_out, adder_11_out, adder_12_out, adder_13_out, adder_14_out,
       adder_15_out;

  Subtractor #(.width(7)) subtractor_1 (.a(ASCII_CODE), .b(7'b0100000), .out(subtractor_1_out));  // open: bin, bout
  Adder #(.width(11)) adder_1 (.a({4'b0000, subtractor_1_out}), .b(11'h1), .out(adder_1_out));  // open: cin, cout
  Adder #(.width(11)) adder_2 (.a(adder_1_out), .b(11'h1), .out(adder_2_out));  // open: cin, cout
  Adder #(.width(11)) adder_3 (.a(adder_2_out), .b(11'h1), .out(adder_3_out));  // open: cin, cout
  Adder #(.width(11)) adder_4 (.a(adder_3_out), .b(11'h1), .out(adder_4_out));  // open: cin, cout
  Adder #(.width(11)) adder_5 (.a(adder_4_out), .b(11'h1), .out(adder_5_out));  // open: cin, cout
  Adder #(.width(11)) adder_6 (.a(adder_5_out), .b(11'h1), .out(adder_6_out));  // open: cin, cout
  Adder #(.width(11)) adder_7 (.a(adder_6_out), .b(11'h1), .out(adder_7_out));  // open: cin, cout
  Adder #(.width(11)) adder_8 (.a(adder_7_out), .b(11'h1), .out(adder_8_out));  // open: cin, cout
  Adder #(.width(11)) adder_9 (.a(adder_8_out), .b(11'h1), .out(adder_9_out));  // open: cin, cout
  Adder #(.width(11)) adder_10 (.a(adder_9_out), .b(11'h1), .out(adder_10_out));  // open: cin, cout
  Adder #(.width(11)) adder_11 (.a(adder_10_out), .b(11'h1), .out(adder_11_out));  // open: cin, cout
  Adder #(.width(11)) adder_12 (.a(adder_11_out), .b(11'h1), .out(adder_12_out));  // open: cin, cout
  Adder #(.width(11)) adder_13 (.a(adder_12_out), .b(11'h1), .out(adder_13_out));  // open: cin, cout
  Adder #(.width(11)) adder_14 (.a(adder_13_out), .b(11'h1), .out(adder_14_out));  // open: cin, cout
  Adder #(.width(11)) adder_15 (.a(adder_14_out), .b(11'h1), .out(adder_15_out));  // open: cin, cout
  ROM #(.addrWidth(11), .Select("high")) rom_1 (.addr({4'b0000, subtractor_1_out}), .data(row1), .sel(1'b1));
  ROM #(.addrWidth(11), .Select("high")) rom_2 (.addr(adder_1_out), .data(row2), .sel(1'b1));
  ROM #(.addrWidth(11), .Select("high")) rom_3 (.addr(adder_2_out), .data(row3), .sel(1'b1));
  ROM #(.addrWidth(11), .Select("high")) rom_4 (.addr(adder_3_out), .data(row4), .sel(1'b1));
  ROM #(.addrWidth(11), .Select("high")) rom_5 (.addr(adder_4_out), .data(row5), .sel(1'b1));
  ROM #(.addrWidth(11), .Select("high")) rom_6 (.addr(adder_5_out), .data(row6), .sel(1'b1));
  ROM #(.addrWidth(11), .Select("high")) rom_7 (.addr(adder_6_out), .data(row7), .sel(1'b1));
  ROM #(.addrWidth(11), .Select("high")) rom_8 (.addr(adder_7_out), .data(row8), .sel(1'b1));
  ROM #(.addrWidth(11), .Select("high")) rom_9 (.addr(adder_8_out), .data(row9), .sel(1'b1));
  ROM #(.addrWidth(11), .Select("high")) rom_10 (.addr(adder_9_out), .data(row10), .sel(1'b1));
  ROM #(.addrWidth(11), .Select("high")) rom_11 (.addr(adder_10_out), .data(row11), .sel(1'b1));
  ROM #(.addrWidth(11), .Select("high")) rom_12 (.addr(adder_11_out), .data(row12), .sel(1'b1));
  ROM #(.addrWidth(11), .Select("high")) rom_13 (.addr(adder_12_out), .data(row13), .sel(1'b1));
  ROM #(.addrWidth(11), .Select("high")) rom_14 (.addr(adder_13_out), .data(row14), .sel(1'b1));
  ROM #(.addrWidth(11), .Select("high")) rom_15 (.addr(adder_14_out), .data(row15), .sel(1'b1));
  ROM #(.addrWidth(11), .Select("high")) rom_16 (.addr(adder_15_out), .data(row16), .sel(1'b1));
  DotMatrix #(.inputtype("row"), .matrixcols(8), .matrixrows(16)) dotmatrix_1 (
    .row0(row1), .row1(row2), .row2(row3), .row3(row4), .row4(row5), .row5(row6), .row6(row7), .row7(row8),
    .row8(row9), .row9(row10), .row10(row11), .row11(row12), .row12(row13), .row13(row14), .row14(row15),
    .row15(row16));

  // Other names for the same wires on the sheet: Code[6:0] = ASCII_CODE

  // Notes on the sheet:
  //   ASCII编码
  //   输入引脚
  //   输出引脚
  //   contents of rom_1 (hex, n*v repeats v):
  //   0 0 63 63 73 7b 7f 6f 67 63 63 63 6*0 f 6*6 66 66 3c 6*0 9*63 3e 6*0 1e 33 61 4*60 61 33 1e 6*0 3e
  //   63 63 30 1c 6 3 63 63 3e 6*0 63 63 73 7b 7f 6f 67 63 63 63 6*0 f 6*6 66 66 3c 6*0 9*63 3e
  //   contents of rom_2 (hex, n*v repeats v):
  //   0 0 63 63 73 7b 7f 6f 67 63 63 63 6*0 f 6*6 66 66 3c 6*0 9*63 3e 6*0 1e 33 61 4*60 61 33 1e 6*0 3e
  //   63 63 30 1c 6 3 63 63 3e 6*0 63 63 73 7b 7f 6f 67 63 63 63 6*0 f 6*6 66 66 3c 6*0 9*63 3e
  //   contents of rom_3 (hex, n*v repeats v):
  //   0 0 63 63 73 7b 7f 6f 67 63 63 63 6*0 f 6*6 66 66 3c 6*0 9*63 3e 6*0 1e 33 61 4*60 61 33 1e 6*0 3e
  //   63 63 30 1c 6 3 63 63 3e 6*0 63 63 73 7b 7f 6f 67 63 63 63 6*0 f 6*6 66 66 3c 6*0 9*63 3e
  //   contents of rom_4 (hex, n*v repeats v):
  //   0 0 63 63 73 7b 7f 6f 67 63 63 63 6*0 f 6*6 66 66 3c 6*0 9*63 3e 6*0 1e 33 61 4*60 61 33 1e 6*0 3e
  //   63 63 30 1c 6 3 63 63 3e 6*0 63 63 73 7b 7f 6f 67 63 63 63 6*0 f 6*6 66 66 3c 6*0 9*63 3e
  //   contents of rom_5 (hex, n*v repeats v):
  //   0 0 63 63 73 7b 7f 6f 67 63 63 63 6*0 f 6*6 66 66 3c 6*0 9*63 3e 6*0 1e 33 61 4*60 61 33 1e 6*0 3e
  //   63 63 30 1c 6 3 63 63 3e 6*0 63 63 73 7b 7f 6f 67 63 63 63 6*0 f 6*6 66 66 3c 6*0 9*63 3e
  //   contents of rom_6 (hex, n*v repeats v):
  //   0 0 63 63 73 7b 7f 6f 67 63 63 63 6*0 f 6*6 66 66 3c 6*0 9*63 3e 6*0 1e 33 61 4*60 61 33 1e 6*0 3e
  //   63 63 30 1c 6 3 63 63 3e 6*0 63 63 73 7b 7f 6f 67 63 63 63 6*0 f 6*6 66 66 3c 6*0 9*63 3e
  //   contents of rom_7 (hex, n*v repeats v):
  //   0 0 63 63 73 7b 7f 6f 67 63 63 63 6*0 f 6*6 66 66 3c 6*0 9*63 3e 6*0 1e 33 61 4*60 61 33 1e 6*0 3e
  //   63 63 30 1c 6 3 63 63 3e 6*0 63 63 73 7b 7f 6f 67 63 63 63 6*0 f 6*6 66 66 3c 6*0 9*63 3e
  //   contents of rom_8 (hex, n*v repeats v):
  //   0 0 63 63 73 7b 7f 6f 67 63 63 63 6*0 f 6*6 66 66 3c 6*0 9*63 3e 6*0 1e 33 61 4*60 61 33 1e 6*0 3e
  //   63 63 30 1c 6 3 63 63 3e 6*0 63 63 73 7b 7f 6f 67 63 63 63 6*0 f 6*6 66 66 3c 6*0 9*63 3e
  //   contents of rom_9 (hex, n*v repeats v):
  //   0 0 63 63 73 7b 7f 6f 67 63 63 63 6*0 f 6*6 66 66 3c 6*0 9*63 3e 6*0 1e 33 61 4*60 61 33 1e 6*0 3e
  //   63 63 30 1c 6 3 63 63 3e 6*0 63 63 73 7b 7f 6f 67 63 63 63 6*0 f 6*6 66 66 3c 6*0 9*63 3e
  //   contents of rom_10 (hex, n*v repeats v):
  //   0 0 63 63 73 7b 7f 6f 67 63 63 63 6*0 f 6*6 66 66 3c 6*0 9*63 3e 6*0 1e 33 61 4*60 61 33 1e 6*0 3e
  //   63 63 30 1c 6 3 63 63 3e 6*0 63 63 73 7b 7f 6f 67 63 63 63 6*0 f 6*6 66 66 3c 6*0 9*63 3e
  //   contents of rom_11 (hex, n*v repeats v):
  //   0 0 63 63 73 7b 7f 6f 67 63 63 63 6*0 f 6*6 66 66 3c 6*0 9*63 3e 6*0 1e 33 61 4*60 61 33 1e 6*0 3e
  //   63 63 30 1c 6 3 63 63 3e 6*0 63 63 73 7b 7f 6f 67 63 63 63 6*0 f 6*6 66 66 3c 6*0 9*63 3e
  //   contents of rom_12 (hex, n*v repeats v):
  //   0 0 63 63 73 7b 7f 6f 67 63 63 63 6*0 f 6*6 66 66 3c 6*0 9*63 3e 6*0 1e 33 61 4*60 61 33 1e 6*0 3e
  //   63 63 30 1c 6 3 63 63 3e 6*0 63 63 73 7b 7f 6f 67 63 63 63 6*0 f 6*6 66 66 3c 6*0 9*63 3e
  //   contents of rom_13 (hex, n*v repeats v):
  //   0 0 63 63 73 7b 7f 6f 67 63 63 63 6*0 f 6*6 66 66 3c 6*0 9*63 3e 6*0 1e 33 61 4*60 61 33 1e 6*0 3e
  //   63 63 30 1c 6 3 63 63 3e 6*0 63 63 73 7b 7f 6f 67 63 63 63 6*0 f 6*6 66 66 3c 6*0 9*63 3e
  //   contents of rom_14 (hex, n*v repeats v):
  //   0 0 63 63 73 7b 7f 6f 67 63 63 63 6*0 f 6*6 66 66 3c 6*0 9*63 3e 6*0 1e 33 61 4*60 61 33 1e 6*0 3e
  //   63 63 30 1c 6 3 63 63 3e 6*0 63 63 73 7b 7f 6f 67 63 63 63 6*0 f 6*6 66 66 3c 6*0 9*63 3e
  //   contents of rom_15 (hex, n*v repeats v):
  //   0 0 63 63 73 7b 7f 6f 67 63 63 63 6*0 f 6*6 66 66 3c 6*0 9*63 3e 6*0 1e 33 61 4*60 61 33 1e 6*0 3e
  //   63 63 30 1c 6 3 63 63 3e 6*0 63 63 73 7b 7f 6f 67 63 63 63 6*0 f 6*6 66 66 3c 6*0 9*63 3e
  //   contents of rom_16 (hex, n*v repeats v):
  //   0 0 63 63 73 7b 7f 6f 67 63 63 63 6*0 f 6*6 66 66 3c 6*0 9*63 3e 6*0 1e 33 61 4*60 61 33 1e 6*0 3e
  //   63 63 30 1c 6 3 63 63 3e 6*0 63 63 73 7b 7f 6f 67 63 63 63 6*0 f 6*6 66 66 3c 6*0 9*63 3e
endmodule

module \灯  (
);

  wire clock_1_out;
  wire [6:0] adder_1_out, adder_2_out, adder_3_out, counter_1_q;
  wire [7:0] main_1_row1, main_1_row2, main_1_row3, main_1_row4, main_1_row5, main_1_row6, main_1_row7,
       main_1_row8, main_1_row9, main_1_row10, main_1_row11, main_1_row12, main_1_row13, main_1_row14,
       main_1_row15, main_1_row16, main_2_row1, main_2_row2, main_2_row3, main_2_row4, main_2_row5,
       main_2_row6, main_2_row7, main_2_row8, main_2_row9, main_2_row10, main_2_row11, main_2_row12,
       main_2_row13, main_2_row14, main_2_row15, main_2_row16, main_3_row1, main_3_row2, main_3_row3,
       main_3_row4, main_3_row5, main_3_row6, main_3_row7, main_3_row8, main_3_row9, main_3_row10,
       main_3_row11, main_3_row12, main_3_row13, main_3_row14, main_3_row15, main_3_row16;

  Counter #(.width(7), .max('h50)) counter_1 (
    .Q(counter_1_q), .clk(clock_1_out));  // open: load, D, count, carry, clr, preset, down
  Clock clock_1 (.out(clock_1_out));
  Adder #(.width(7)) adder_1 (.a(counter_1_q), .b(7'b0100000), .out(adder_1_out));  // open: cin, cout
  Adder #(.width(7)) adder_2 (.a(adder_1_out), .b(7'b0010000), .out(adder_2_out));  // open: cin, cout
  Adder #(.width(7)) adder_3 (.a(adder_2_out), .b(7'b0010000), .out(adder_3_out));  // open: cin, cout
  main main_1 (
    .ASCII_CODE(adder_1_out), .row1(main_1_row1), .row2(main_1_row2), .row3(main_1_row3), .row4(main_1_row4),
    .row7(main_1_row7), .row5(main_1_row5), .row6(main_1_row6), .row8(main_1_row8), .row9(main_1_row9),
    .row10(main_1_row10), .row11(main_1_row11), .row12(main_1_row12), .row13(main_1_row13),
    .row14(main_1_row14), .row15(main_1_row15), .row16(main_1_row16));
  main main_2 (
    .ASCII_CODE(adder_2_out), .row1(main_2_row1), .row2(main_2_row2), .row3(main_2_row3), .row4(main_2_row4),
    .row7(main_2_row7), .row5(main_2_row5), .row6(main_2_row6), .row8(main_2_row8), .row9(main_2_row9),
    .row10(main_2_row10), .row11(main_2_row11), .row12(main_2_row12), .row13(main_2_row13),
    .row14(main_2_row14), .row15(main_2_row15), .row16(main_2_row16));
  main main_3 (
    .ASCII_CODE(adder_3_out), .row1(main_3_row1), .row2(main_3_row2), .row3(main_3_row3), .row4(main_3_row4),
    .row7(main_3_row7), .row5(main_3_row5), .row6(main_3_row6), .row8(main_3_row8), .row9(main_3_row9),
    .row10(main_3_row10), .row11(main_3_row11), .row12(main_3_row12), .row13(main_3_row13),
    .row14(main_3_row14), .row15(main_3_row15), .row16(main_3_row16));
  DotMatrix #(.inputtype("row"), .matrixcols(8), .matrixrows(16)) dotmatrix_1 (
    .row0(main_1_row1), .row1(main_1_row2), .row2(main_1_row3), .row3(main_1_row4), .row4(main_1_row5),
    .row5(main_1_row6), .row6(main_1_row7), .row7(main_1_row8), .row8(main_1_row9), .row9(main_1_row10),
    .row10(main_1_row11), .row11(main_1_row12), .row12(main_1_row13), .row13(main_1_row14),
    .row14(main_1_row15), .row15(main_1_row16));
  DotMatrix #(.inputtype("row"), .matrixcols(8), .matrixrows(16)) dotmatrix_2 (
    .row0(main_2_row1), .row1(main_2_row2), .row2(main_2_row3), .row3(main_2_row4), .row4(main_2_row5),
    .row5(main_2_row6), .row6(main_2_row7), .row7(main_2_row8), .row8(main_2_row9), .row9(main_2_row10),
    .row10(main_2_row11), .row11(main_2_row12), .row12(main_2_row13), .row13(main_2_row14),
    .row14(main_2_row15), .row15(main_2_row16));
  DotMatrix #(.inputtype("row"), .matrixcols(8), .matrixrows(16)) dotmatrix_3 (
    .row0(main_3_row1), .row1(main_3_row2), .row2(main_3_row3), .row3(main_3_row4), .row4(main_3_row5),
    .row5(main_3_row6), .row6(main_3_row7), .row7(main_3_row8), .row8(main_3_row9), .row9(main_3_row10),
    .row10(main_3_row11), .row11(main_3_row12), .row12(main_3_row13), .row13(main_3_row14),
    .row14(main_3_row15), .row15(main_3_row16));
endmodule
