// Logisim project lab5.2.circ as structural Verilog: 3 circuits, main circuit DataRam
module Err (
  input  [2:0] in_1,
  input  in_2,
  output out_3
);

  wire comparator_1_eq, comparator_2_eq, comparator_3_eq, comparator_4_eq, comparator_5_eq, not_1_out,
       or_1_out;

  Comparator #(.width(3), .mode("unsigned")) comparator_1 (.a(in_1), .b(3'b000), .eq(comparator_1_eq));  // open: gt, lt
  Comparator #(.width(3), .mode("unsigned")) comparator_2 (.a(in_1), .b(3'b001), .eq(comparator_2_eq));  // open: gt, lt
  Comparator #(.width(3), .mode("unsigned")) comparator_3 (.a(in_1), .b(3'b010), .eq(comparator_3_eq));  // open: gt, lt
  Comparator #(.width(3), .mode("unsigned")) comparator_4 (.a(in_1), .b(3'b101), .eq(comparator_4_eq));  // open: gt, lt
  Comparator #(.width(3), .mode("unsigned")) comparator_5 (.a(in_1), .b(3'b110), .eq(comparator_5_eq));  // open: gt, lt
  or or_1 (or_1_out, comparator_1_eq, comparator_2_eq, comparator_3_eq, comparator_4_eq, comparator_5_eq);
  not not_1 (not_1_out, or_1_out);
  or or_2 (out_3, not_1_out, in_2);

  // Other names for the same wires on the sheet: r = out_3; t = in_2; tunnel[2:0] = in_1
endmodule

// DataRAM
module DataRam (
  input  CLK,
  input  CLR,
  input  WE,
  input  [2:0] MemOp,
  input  [17:0] Addr,
  input  [31:0] Din,
  output AlignErr,
  output [31:0] DataOut
);

  wire and_1_out, and_2_out, and_3_out, and_4_out, and_5_out;
  wire [1:0] sel_1_out_4;
  wire [1:1] sel_1_out_6;
  wire [2:2] sel_1_out_7;
  wire [7:0] multiplexer_1_out, multiplexer_2_out, multiplexer_3_out, multiplexer_4_out;
  wire [15:0] multiplexer_5_out;
  wire [31:0] bit_extender_1_out, bit_extender_2_out, bit_extender_3_out, bit_extender_4_out,
       multiplexer_6_out, ram_1_data;

  Sel sel_1 (
    .in_1(MemOp), .out_4(sel_1_out_4[0]), .out_5(sel_1_out_4[1]), .in_2(Addr[0]), .out_6(sel_1_out_6[1]),
    .in_3(Addr[1]), .out_7(sel_1_out_7[2]));
  Err err_1 (.in_1(MemOp), .in_2(and_1_out), .out_3(AlignErr));
  and and_1 (and_1_out, ~sel_1_out_4[0], ~sel_1_out_4[1], ~sel_1_out_6[1], ~sel_1_out_7[2]);  // AND_Gate
  and and_2 (and_2_out, WE, sel_1_out_4[0]);
  Multiplexer #(.select(2), .width(8), .enable("false")) multiplexer_1 (
    .in2(Din[7:0]), .in3(Din[15:8]), .out(multiplexer_1_out), .sel(sel_1_out_4));  // open: in0, in1
  and and_3 (and_3_out, WE, sel_1_out_4[1]);
  Multiplexer #(.select(2), .width(8), .enable("false")) multiplexer_2 (
    .in2(Din[7:0]), .in3(Din[23:16]), .out(multiplexer_2_out), .sel({sel_1_out_6[1], sel_1_out_4[1]}));  // open: in0, in1
  and and_4 (and_4_out, WE, sel_1_out_6[1]);
  Multiplexer #(.select(3), .width(8), .enable("false")) multiplexer_3 (
    .in4(Din[7:0]), .in6(Din[15:8]), .in7(Din[31:24]), .out(multiplexer_3_out),
    .sel({sel_1_out_7[2], sel_1_out_6[1], sel_1_out_4[1]}));  // open: in0, in1, in2, in3, in5
  and and_5 (and_5_out, WE, sel_1_out_7[2]);
  RAM #(.addrWidth(18), .bus("separate"), .Select("high")) ram_1 (
    .addr({Addr[17:2], 2'b00}), .din(Din[7:0]), .data(ram_1_data[7:0]), .str(and_2_out), .clk(CLK),
    .ld(sel_1_out_4[0]), .clr(CLR));  // open: sel
  RAM #(.addrWidth(18), .bus("separate"), .Select("high")) ram_2 (
    .addr({Addr[17:2], 2'b00}), .din(multiplexer_1_out), .data(ram_1_data[15:8]), .str(and_3_out), .clk(CLK),
    .ld(sel_1_out_4[1]), .clr(CLR));  // open: sel
  RAM #(.addrWidth(18), .bus("separate"), .Select("high")) ram_3 (
    .addr({Addr[17:2], 2'b00}), .din(multiplexer_2_out), .data(ram_1_data[23:16]), .str(and_4_out),
    .clk(CLK), .ld(sel_1_out_6[1]), .clr(CLR));  // open: sel
  RAM #(.addrWidth(18), .bus("separate"), .Select("high")) ram_4 (
    .addr({Addr[17:2], 2'b00}), .din(multiplexer_3_out), .data(ram_1_data[31:24]), .str(and_5_out),
    .clk(CLK), .ld(sel_1_out_7[2]), .clr(CLR));  // open: sel
  Multiplexer #(.select(2), .width(8), .enable("false")) multiplexer_4 (
    .in0(ram_1_data[7:0]), .in1(ram_1_data[15:8]), .in2(ram_1_data[23:16]), .in3(ram_1_data[31:24]),
    .out(multiplexer_4_out), .sel(Addr[1:0]));
  Multiplexer #(.select(2), .width(16), .enable("false")) multiplexer_5 (
    .in0(ram_1_data[15:0]), .in2(ram_1_data[31:16]), .out(multiplexer_5_out), .sel(Addr[1:0]));  // open: in1, in3
  assign bit_extender_1_out = {{24{1'b0}}, multiplexer_4_out};  // Bit_Extender bit_extender_1
  assign bit_extender_2_out = {{16{1'b0}}, multiplexer_5_out};  // Bit_Extender bit_extender_2
  assign bit_extender_3_out = {{24{multiplexer_4_out[7]}}, multiplexer_4_out};  // Bit_Extender bit_extender_3
  assign bit_extender_4_out = {{16{multiplexer_5_out[15]}}, multiplexer_5_out};  // Bit_Extender bit_extender_4
  Multiplexer #(.select(3), .width(32), .enable("false")) multiplexer_6 (
    .in0(ram_1_data), .in1(bit_extender_1_out), .in2(bit_extender_2_out), .in5(bit_extender_3_out),
    .in6(bit_extender_4_out), .out(multiplexer_6_out), .sel(MemOp));  // open: in3, in4, in7
  Multiplexer #(.width(32), .enable("false")) multiplexer_7 (
    .in0(multiplexer_6_out), .out(DataOut), .sel(AlignErr));  // open: in1

  // Other names for the same wires on the sheet: Dout[31:0] = DataOut

  // Notes on the sheet:
  //   输入引脚
  //   请勿修改引脚名称、电路名称及电路封装外观
  //   为了后续实验中的引用，不要修改MemOp的编码定义、引脚名称和在布局中的位置。
  //   32位数据存储器，按字节分4片存储，可按照字节、半字和字进行存储；读取字节或半字时，支持0扩展和符号位扩展。
  //   输出引脚
endmodule

module Sel (
  input  [2:0] in_1,
  input  in_2,
  input  in_3,
  output out_4,
  output out_5,
  output out_6,
  output out_7
);

  wire and_1_out, and_2_out, and_3_out, and_4_out, and_5_out, and_6_out, and_7_out;

  and and_1 (and_1_out, ~in_1[0], ~in_1[1], ~in_1[2], ~in_2, ~in_3);  // AND_Gate
  and and_2 (and_2_out, ~in_1[1], in_1[0], in_2, in_3);  // AND_Gate
  and and_3 (and_3_out, in_1[1], ~in_1[0], in_3, ~in_2);  // AND_Gate
  and and_4 (and_4_out, ~in_1[1], in_1[0], in_3, ~in_2);  // AND_Gate
  and and_5 (and_5_out, ~in_1[1], in_1[0], ~in_3, in_2);  // AND_Gate
  and and_6 (and_6_out, in_1[1], ~in_1[0], ~in_3, ~in_2);  // AND_Gate
  and and_7 (and_7_out, ~in_1[1], in_1[0], ~in_2, ~in_3);  // AND_Gate
  or or_1 (out_7, and_1_out, and_2_out, and_3_out);
  or or_2 (out_6, and_1_out, and_4_out, and_3_out);
  or or_3 (out_5, and_1_out, and_5_out, and_6_out);
  or or_4 (out_4, and_1_out, and_7_out, and_6_out);

  // Other names for the same wires on the sheet: addr0 = in_2; addr1 = in_3; Op[2:0] = in_1; sel0 = out_4;
  //   sel1 = out_5; sel2 = out_6; sel3 = out_7
endmodule
