// Logisim project lab6.1.circ as structural Verilog: 1 circuit, main circuit 控制器
module \控制器  (
  input  [6:0] opcode,
  input  [2:0] funct3,
  input  [6:0] funct7,
  output [2:0] ExtOp,
  output RegWr,
  output [2:0] Branch,
  output ALUASrc,
  output [1:0] ALUBSrc,
  output [3:0] ALUctr,
  output MemtoReg,
  output [2:0] MemOp,
  output MemWr
);

  wire add, addi, \and , andi, auipc, B_out, beq, bge, bgeu, blt, bltu, bne, comparator_1_eq,
       comparator_2_eq, comparator_3_eq, comparator_4_eq, comparator_5_eq, comparator_6_eq, comparator_7_eq,
       comparator_8_eq, comparator_9_eq, comparator_10_eq, comparator_11_eq, comparator_12_eq,
       comparator_13_eq, I0_out, I1_out, I2_out, jalr, lb, lbu, lh, lhu, lui, lw, \or , or_1_out, or_2_out,
       or_4_out, or_5_out, or_6_out, or_14_out, or_16_out, or_19_out, or_20_out, or_25_out, or_28_out,
       or_30_out, ori, R_out, S_out, sb, sh, sll, slli, slt, slti, sltiu, sltu, sra, srai, srl, srli, sub,
       sw, \xor , xori;

  and U0 (lui, ~opcode[6], opcode[5], opcode[4], ~opcode[3], opcode[2], opcode[1], opcode[0]);  // AND_Gate
  and U1 (auipc, ~opcode[6], ~opcode[5], opcode[4], ~opcode[3], opcode[2], opcode[1], opcode[0]);  // AND_Gate
  and I0 (I0_out, ~opcode[6], ~opcode[5], opcode[4], ~opcode[3], ~opcode[2], opcode[1], opcode[0]);  // AND_Gate
  and I1 (I1_out, opcode[6], opcode[5], ~opcode[4], ~opcode[3], opcode[2], opcode[1], opcode[0]);  // AND_Gate
  and I2 (I2_out, ~opcode[6], ~opcode[5], ~opcode[4], ~opcode[3], ~opcode[2], opcode[1], opcode[0]);  // AND_Gate
  and J (ExtOp[2], opcode[6], opcode[5], ~opcode[4], opcode[3], opcode[2], opcode[1], opcode[0]);  // AND_Gate
  and R (R_out, ~opcode[6], opcode[5], opcode[4], ~opcode[3], ~opcode[2], opcode[1], opcode[0]);  // AND_Gate
  and B (B_out, opcode[6], opcode[5], ~opcode[4], ~opcode[3], ~opcode[2], opcode[1], opcode[0]);  // AND_Gate
  and S (S_out, ~opcode[6], opcode[5], ~opcode[4], ~opcode[3], ~opcode[2], opcode[1], opcode[0]);  // AND_Gate
  or or_1 (or_1_out, lui, auipc, beq);
  or or_2 (or_2_out, bne, blt, bge, bltu, bgeu);
  or or_3 (ExtOp[0], or_1_out, or_2_out);
  or or_4 (or_4_out, beq, bne, blt);
  or or_5 (or_5_out, bge, bltu, bgeu);
  or or_6 (or_6_out, sb, sh, sw);
  or or_7 (ExtOp[1], or_4_out, or_5_out, or_6_out);
  or or_8 (ALUASrc, auipc, ExtOp[2], jalr);
  Comparator #(.width(3), .mode("unsigned")) comparator_1 (
    .a(funct3), .b(3'b000), .eq(comparator_1_eq));  // open: gt, lt
  and and_1 (jalr, I1_out, comparator_1_eq);
  and and_2 (lb, I2_out, comparator_1_eq);
  or or_9 (ALUBSrc[0], ExtOp[2], jalr);
  Comparator #(.width(1), .mode("unsigned")) comparator_2 (
    .a(funct7[5]), .b(1'b0), .eq(comparator_2_eq));  // open: gt, lt
  and and_3 (addi, I0_out, comparator_1_eq);
  or or_10 (ALUBSrc[1], lui, auipc, addi, slti, sltiu, xori, ori, andi, slli, srli, srai, lb, lh, lw, lbu, lhu, sb, sh, sw);
  and and_4 (add, R_out, comparator_1_eq, comparator_2_eq);
  and and_5 (slti, I0_out, comparator_3_eq);
  Comparator #(.width(3), .mode("unsigned")) comparator_3 (
    .a(funct3), .b(3'b010), .eq(comparator_3_eq));  // open: gt, lt
  and and_6 (lw, I2_out, comparator_3_eq);
  and and_7 (beq, B_out, comparator_1_eq);
  and and_8 (sb, S_out, comparator_1_eq);
  or or_11 (ALUctr[0], lui, sltiu, andi, slli, srli, srai, sll, sltu, srl, sra, \and , bltu, bgeu);
  Comparator #(.width(1), .mode("unsigned")) comparator_4 (
    .a(funct7[5]), .b(1'b1), .eq(comparator_4_eq));  // open: gt, lt
  and and_9 (slt, R_out, comparator_3_eq, comparator_2_eq);
  and and_10 (sltiu, I0_out, comparator_5_eq);
  Comparator #(.width(3), .mode("unsigned")) comparator_5 (
    .a(funct3), .b(3'b011), .eq(comparator_5_eq));  // open: gt, lt
  and and_11 (sw, S_out, comparator_3_eq);
  or or_12 (ALUctr[1], lui, slti, sltiu, ori, andi, slt, sltu, \or , \and , beq, bne, blt, bge, bltu, bgeu);
  and and_12 (sub, R_out, comparator_1_eq, comparator_4_eq);
  Comparator #(.width(3), .mode("unsigned")) comparator_6 (
    .a(funct3), .b(3'b100), .eq(comparator_6_eq));  // open: gt, lt
  and and_13 (sltu, R_out, comparator_5_eq, comparator_2_eq);
  or or_13 (ALUctr[2], lui, xori, ori, andi, srli, srai, \xor , srl, sra, \or , \and );
  and and_14 (xori, I0_out, comparator_6_eq);
  and and_15 (lbu, I2_out, comparator_6_eq);
  or or_14 (or_14_out, lui, srai, sub);
  or or_15 (ALUctr[3], or_14_out, sra);
  Comparator #(.width(3), .mode("unsigned")) comparator_7 (
    .a(funct3), .b(3'b110), .eq(comparator_7_eq));  // open: gt, lt
  and and_16 (\xor , R_out, comparator_6_eq, comparator_2_eq);
  and and_17 (blt, comparator_6_eq, B_out);
  or or_16 (or_16_out, ExtOp[2], bne, bge);
  or or_17 (Branch[1], jalr, blt, bge, bltu, bgeu);
  or or_18 (Branch[0], or_16_out, bgeu);
  and and_18 (ori, I0_out, comparator_7_eq);
  and and_19 (\or , R_out, comparator_7_eq, comparator_2_eq);
  and and_20 (bltu, comparator_7_eq, B_out);
  or or_19 (or_19_out, bge, bltu, bgeu);
  or or_20 (or_20_out, beq, bne, blt);
  or or_21 (Branch[2], or_20_out, or_19_out);
  Comparator #(.width(3), .mode("unsigned")) comparator_8 (
    .a(funct3), .b(3'b111), .eq(comparator_8_eq));  // open: gt, lt
  or or_22 (MemtoReg, lb, lh, lw, lbu, lhu);
  and and_21 (andi, I0_out, comparator_8_eq);
  and and_22 (\and , comparator_8_eq, R_out, comparator_2_eq);
  and and_23 (bgeu, comparator_8_eq, B_out);
  or or_23 (MemOp[0], lb, lbu, sb);
  or or_24 (MemWr, sb, sh, sw);
  Comparator #(.width(1), .mode("unsigned")) comparator_9 (
    .a(funct7[5]), .b(1'b0), .eq(comparator_9_eq));  // open: gt, lt
  Comparator #(.width(3), .mode("unsigned")) comparator_10 (
    .a(funct3), .b(3'b001), .eq(comparator_10_eq));  // open: gt, lt
  or or_25 (or_25_out, lb, lh, sb);
  or or_26 (MemOp[1], lh, lhu, sh);
  or or_27 (MemOp[2], or_25_out, sh);
  and and_24 (slli, I0_out, comparator_9_eq, comparator_10_eq);
  and and_25 (lh, comparator_10_eq, I2_out);
  and and_26 (sll, R_out, comparator_10_eq, comparator_2_eq);
  or or_28 (or_28_out, lui, auipc, addi, slti, sltiu, xori, ori, andi, slli, srli, srai, add, sub);
  and and_27 (bne, B_out, comparator_10_eq);
  and and_28 (sh, S_out, comparator_10_eq);
  or or_29 (RegWr, or_28_out, or_30_out);
  Comparator #(.width(3), .mode("unsigned")) comparator_11 (
    .a(funct3), .b(3'b101), .eq(comparator_11_eq));  // open: gt, lt
  and and_29 (lhu, I2_out, comparator_11_eq);
  or or_30 (or_30_out, sll, slt, sltu, \xor , srl, sra, \or , \and , ExtOp[2], jalr, lb, lh, lw, lbu, lhu);
  and and_30 (srli, I0_out, comparator_9_eq, comparator_11_eq);
  and and_31 (bge, B_out, comparator_11_eq);
  Comparator #(.width(1), .mode("unsigned")) comparator_12 (
    .a(funct7[5]), .b(1'b1), .eq(comparator_12_eq));  // open: gt, lt
  Comparator #(.width(3), .mode("unsigned")) comparator_13 (
    .a(funct3), .b(3'b101), .eq(comparator_13_eq));  // open: gt, lt
  and and_32 (srl, R_out, comparator_11_eq, comparator_2_eq);
  and and_33 (sra, R_out, comparator_11_eq, comparator_4_eq);
  and and_34 (srai, I0_out, comparator_12_eq, comparator_13_eq);

  // Other names for the same wires on the sheet: jal = ExtOp[2]

  // Notes on the sheet:
  //   输入引脚
  //   请勿修改引脚名称、电路名称及电路封装外观
  //   提示：根据指令种类，把7位指令code用一位指令类型标志位来表示，再通过功能码来区分具体指令，生成控制信号。
  //   输出引脚
endmodule
