// Logisim project lab6.1.false.circ as structural Verilog: 1 circuit, main circuit 控制器
module \控制器  (
  input  [6:0] opcode,
  input  [2:0] funct3,
  input  [6:0] funct7,
  output [2:0] ExtOp,
  output RegWr,
  output [2:0] Branch,
  output ALUASrc,
  output [1:0] ALUBSrc,
  output [3:0] ALUctr,
  output MemtoReg,
  output [2:0] MemOp,
  output MemWr
);

  wire and_1_out, and_2_out, and_3_out, and_4_out, and_6_out, and_7_out, and_8_out, and_9_out, and_10_out,
       and_11_out, and_12_out, and_13_out, and_14_out, and_15_out, and_16_out, and_17_out, and_18_out,
       comparator_1_eq, comparator_2_eq, comparator_3_eq, comparator_4_eq, comparator_5_eq, comparator_6_eq,
       comparator_7_eq, comparator_8_eq, comparator_9_eq, comparator_10_eq, comparator_11_eq,
       comparator_12_eq, comparator_13_eq, comparator_14_gt, I_out, or_1_out, or_2_out, or_11_out, or_12_out,
       or_13_out, or_14_out, or_15_out, or_16_out, or_20_out, or_21_out, or_23_out, R_out, U_out;

  and and_1 (and_1_out, ~opcode[6], opcode[5], opcode[4], ~opcode[3], opcode[2], opcode[1], opcode[0]);  // AND_Gate
  and and_2 (and_2_out, ~opcode[6], ~opcode[5], opcode[4], ~opcode[3], opcode[2], opcode[1], opcode[0]);  // AND_Gate
  and and_3 (and_3_out, ~opcode[6], ~opcode[5], opcode[4], ~opcode[3], ~opcode[2], opcode[1], opcode[0]);  // AND_Gate
  and and_4 (and_4_out, opcode[6], opcode[5], ~opcode[4], ~opcode[3], opcode[2], opcode[1], opcode[0]);  // AND_Gate
  and and_5 (MemtoReg, ~opcode[6], ~opcode[5], ~opcode[4], ~opcode[3], ~opcode[2], opcode[1], opcode[0]);  // AND_Gate
  and J (ExtOp[2], opcode[6], opcode[5], ~opcode[4], opcode[3], opcode[2], opcode[1], opcode[0]);  // AND_Gate
  and R (R_out, ~opcode[6], opcode[5], opcode[4], ~opcode[3], ~opcode[2], opcode[1], opcode[0]);  // AND_Gate
  and B (Branch[2], opcode[6], opcode[5], ~opcode[4], ~opcode[3], ~opcode[2], opcode[1], opcode[0]);  // AND_Gate
  and S (MemWr, ~opcode[6], opcode[5], ~opcode[4], ~opcode[3], ~opcode[2], opcode[1], opcode[0]);  // AND_Gate
  or U (U_out, and_1_out, and_2_out);
  or I (I_out, and_3_out, and_4_out, MemtoReg);
  Comparator #(.width(3), .mode("unsigned")) comparator_1 (
    .a(funct3), .b(3'b001), .eq(comparator_1_eq));  // open: gt, lt
  or or_1 (or_1_out, comparator_1_eq, comparator_2_eq, comparator_3_eq);
  Comparator #(.width(3), .mode("unsigned")) comparator_2 (
    .a(funct3), .b(3'b101), .eq(comparator_2_eq));  // open: gt, lt
  Comparator #(.width(3), .mode("unsigned")) comparator_3 (
    .a(funct3), .b(3'b111), .eq(comparator_3_eq));  // open: gt, lt
  Comparator #(.width(3), .mode("unsigned")) comparator_4 (
    .a(funct3), .b(3'b100), .eq(comparator_4_eq));  // open: gt, lt
  or or_2 (or_2_out, comparator_4_eq, comparator_5_eq, comparator_6_eq, comparator_7_eq);
  Comparator #(.width(3), .mode("unsigned")) comparator_5 (
    .a(funct3), .b(3'b101), .eq(comparator_5_eq));  // open: gt, lt
  Comparator #(.width(3), .mode("unsigned")) comparator_6 (
    .a(funct3), .b(3'b110), .eq(comparator_6_eq));  // open: gt, lt
  Comparator #(.width(3), .mode("unsigned")) comparator_7 (
    .a(funct3), .b(3'b111), .eq(comparator_7_eq));  // open: gt, lt
  or or_3 (RegWr, U_out, I_out, ExtOp[2], R_out);
  or or_4 (ExtOp[0], U_out, Branch[2]);
  or or_5 (ExtOp[1], MemWr, Branch[2]);
  or or_6 (ALUBSrc[0], and_4_out, ExtOp[2]);
  or or_7 (ALUBSrc[1], U_out, and_3_out, MemtoReg, MemWr);
  and and_6 (and_6_out, Branch[2], or_1_out);
  and and_7 (and_7_out, Branch[2], or_2_out);
  Comparator #(.width(3), .mode("unsigned")) comparator_8 (
    .a(funct3), .b(3'b000), .eq(comparator_8_eq));  // open: gt, lt
  or or_8 (ALUASrc, and_2_out, and_4_out, ExtOp[2]);
  or or_9 (Branch[0], ExtOp[2], and_6_out);
  or or_10 (Branch[1], and_4_out, and_7_out);
  and and_8 (and_8_out, MemtoReg, comparator_9_eq);
  Comparator #(.width(3), .mode("unsigned")) comparator_9 (
    .a(funct3), .b(3'b100), .eq(comparator_9_eq));  // open: gt, lt
  or or_11 (or_11_out, MemtoReg, MemWr);
  and and_9 (and_9_out, or_11_out, comparator_10_eq);
  Comparator #(.width(3), .mode("unsigned")) comparator_10 (
    .a(funct3), .b(3'b000), .eq(comparator_10_eq));  // open: gt, lt
  and and_10 (and_10_out, MemtoReg, comparator_11_eq);
  Comparator #(.width(3), .mode("unsigned")) comparator_11 (
    .a(funct3), .b(3'b101), .eq(comparator_11_eq));  // open: gt, lt
  or or_12 (or_12_out, MemtoReg, MemWr);
  and and_11 (and_11_out, or_12_out, comparator_12_eq);
  Comparator #(.width(3), .mode("unsigned")) comparator_12 (
    .a(funct3), .b(3'b001), .eq(comparator_12_eq));  // open: gt, lt
  or or_13 (or_13_out, MemtoReg, MemWr);
  and and_12 (and_12_out, or_13_out, comparator_8_eq);
  or or_14 (or_14_out, MemtoReg, MemWr);
  and and_13 (and_13_out, or_14_out, comparator_13_eq);
  Comparator #(.width(3), .mode("unsigned")) comparator_13 (
    .a(funct3), .b(3'b001), .eq(comparator_13_eq));  // open: gt, lt
  or or_15 (or_15_out, and_3_out, R_out);
  or or_16 (or_16_out, and_3_out, R_out);
  or or_17 (MemOp[0], and_8_out, and_9_out);
  or or_18 (MemOp[1], and_10_out, and_11_out);
  or or_19 (MemOp[2], and_12_out, and_13_out);
  or or_20 (or_20_out, and_3_out, R_out);
  Comparator #(.width(3), .mode("unsigned")) comparator_14 (
    .a(funct3), .b(3'b101), .gt(comparator_14_gt));  // open: eq, lt
  and and_14 (and_14_out, funct3[1], or_21_out);
  or or_21 (or_21_out, R_out, and_3_out);
  and and_15 (and_15_out, funct3[2], or_15_out);
  and and_16 (and_16_out, funct3[0], or_20_out);
  or or_22 (ALUctr[0], and_1_out, and_16_out, and_17_out);
  and and_17 (and_17_out, Branch[2], comparator_14_gt);
  or or_23 (or_23_out, and_1_out, Branch[2]);
  or or_24 (ALUctr[1], or_23_out, and_14_out);
  or or_25 (ALUctr[2], and_1_out, and_15_out);
  or or_26 (ALUctr[3], and_1_out, and_18_out);
  and and_18 (and_18_out, funct7[5], or_16_out);

  // Notes on the sheet:
  //   输入引脚
  //   请勿修改引脚名称、电路名称及电路封装外观
  //   提示：根据指令种类，把7位指令code用一位指令类型标志位来表示，再通过功能码来区分具体指令，生成控制信号。
  //   输出引脚
endmodule
