// Logisim project lab6.5.circ as structural Verilog: 18 circuits, main circuit main
module main (
  input  ReSet,
  input  [31:0] Init_Addr,
  output [31:0] PC,
  output [31:0] IR,
  output [31:0] BusW,
  output [31:0] Din,
  output [15:0] Cycles,
  output Halt
);

  wire alu_1_zero, ALUASrc, branch_1_nxtasrc, branch_1_nxtbsrc, clk, clk_out, MemToReg, MemWr, not_2_out,
       RegWr;
  wire [1:0] ALUBSrc;
  wire [2:0] Branch, ExtOp, idu_1_funct3, MemOp;
  wire [3:0] ALUctr;
  wire [6:0] idu_1_funct7, idu_1_opcode;
  wire [31:0] alu_1_s, dataram_1_dataout, idu_1_busa, idu_1_dataa, idu_1_datab, idu_1_imm;

  Clock u_clk (.out(clk_out));
  not not_1 (clk, clk_out);
  \控制器  \u_控制器_1  (
    .opcode(idu_1_opcode), .ExtOp(ExtOp), .RegWr(RegWr), .Branch(Branch), .funct3(idu_1_funct3),
    .ALUASrc(ALUASrc), .ALUBSrc(ALUBSrc), .ALUctr(ALUctr), .funct7(idu_1_funct7), .MemtoReg(MemToReg),
    .MemOp(MemOp), .MemWr(MemWr), .Halt(Halt));
  ROM #(.addrWidth(16), .dataWidth(32), .Select("high")) rom_1 (.addr(PC[17:2]), .data(IR), .sel(1'b1));
  IDU idu_1 (
    .OpCode(idu_1_opcode), .ExtOp(ExtOp), .RegWr(RegWr), .Imm(idu_1_imm), .Funct3(idu_1_funct3),
    .ALUASrc(ALUASrc), .ALUBSrc(ALUBSrc), .Funct7(idu_1_funct7), .CLK(clk), .IR(IR), .BusW(BusW), .PC(PC),
    .DataA(idu_1_dataa), .DataB(idu_1_datab), .BusA(idu_1_busa), .BusB(Din));
  // Probe on Cycles
  Counter #(.width(16), .max('hffff), .behavior("old")) \u_计数器  (
    .count(not_2_out), .Q(Cycles), .clk(clk), .clr(ReSet));  // open: load, D, carry, preset
  not not_2 (not_2_out, Halt);
  IFU ifu_1 (
    .CLK(clk), .Reset(ReSet), .NxtASrc(branch_1_nxtasrc), .NxtBSrc(branch_1_nxtbsrc),
    .Initial_Address(Init_Addr), .Imm(idu_1_imm), .BusA(idu_1_busa), .PC(PC), .halt(Halt));
  Branch branch_1 (
    .Branch(Branch), .NxtASrc(branch_1_nxtasrc), .Zero(alu_1_zero), .NxtBSrc(branch_1_nxtbsrc),
    .Result0(alu_1_s[0]));
  ALU alu_1 (.A(idu_1_dataa), .B(idu_1_datab), .ALUctr(ALUctr), .S(alu_1_s), .Zero(alu_1_zero));
  DataRAM dataram_1 (
    .Addr(alu_1_s[17:0]), .Din(Din), .CLK(clk), .CLR(ReSet), .WE(MemWr), .MemOp(MemOp),
    .DataOut(dataram_1_dataout));  // open: AlignErr
  Multiplexer #(.width(32), .enable("false")) multiplexer_1 (
    .in0(alu_1_s), .in1(dataram_1_dataout), .out(BusW), .sel(MemToReg));

  // Notes on the sheet:
  //   输入引脚
  //   请勿修改引脚名称、电路名称及电路封装外观
  //   指令存储器和数据存储器数据位都是32位，指令存储器编址以字为单位，数据存储器编址以字节为单位。
  //   引用取指令部件、取操作数部件、ALU部件、数据存储器、分支控制器、指令存储器等部件，完成单周期CPU设计。
  //   contents of rom_1 (hex, n*v repeats v):
  //   93 113 193 213 293 313 393 413 493 513 593 613 693 713 793 813 893 913 993 a13 a93 b13 b93 c13 c93
  //   d13 d93 e13 e93 f13 f93 93 113 208733 393 200193 4c771663 100093 100113 208733 200393 300193
  //   4a771a63 300093 700113 208733 a00393 400193 48771e63 93 ffff8137 208733 ffff83b7 500193 48771263
  //   800000b7 113 208733 800003b7 600193 46771663 800000b7 ffff8137 208733 7fff83b7 700193 44771a63 93
  //   8137 fff10113 208733 83b7 fff38393 800193 42771a63 800000b7 fff08093 113 208733 800003b7 fff38393
  //   900193 40771a63 800000b7 fff08093 8137 fff10113 208733 800083b7 ffe38393 a00193 3e771863 800000b7
  //   8137 fff10113 208733 800083b7 fff38393 b00193 3c771863 800000b7 fff08093 ffff8137 208733 7fff83b7
  //   fff38393 c00193 3a771863 93 fff00113 208733 fff00393 d00193 38771c63 fff00093 100113 208733 393
  //   e00193 38771063 fff00093 fff00113 208733 ffe00393 f00193 36771463 100093 80000137 fff10113 208733
  //   800003b7 1000193 34771663 d00093 b00113 2080b3 1800393 1100193 32709a63 e00093 b00113 208133 1900393
  //   1200193 30711e63 d00093 1080b3 1a00393 1300193 30709463 213 d00093 b00113 208733 70313 120213 200293
  //   fe5214e3 1800393 1400193 2c731e63 213 e00093 b00113 208733 13 70313 120213 200293 fe5212e3 1900393
  //   1500193 2a731663 213 f00093 b00113 208733 13 13 70313 120213 200293 fe5210e3 1a00393 1600193
  //   26731c63 213 d00093 b00113 208733 120213 200293 fe5216e3 1800393 1700193 24771863 213 e00093 b00113
  //   13 208733 120213 200293 fe5214e3 1900393 1800193 22771263 213 f00093 b00113 13 13 208733 120213
  //   200293 fe5212e3 1a00393 1900193 1e771a63 213 d00093 13 b00113 208733 120213 200293 fe5214e3 1800393
  //   1a00193 1c771463 213 e00093 13 b00113 13 208733 120213 200293 fe5212e3 1900393 1b00193 18771c63 213
  //   f00093 13 13 b00113 208733 120213 200293 fe5212e3 1a00393 1c00193 16771463 213 b00113 d00093 208733
  //   120213 200293 fe5216e3 1800393 1d00193 14771063 213 b00113 e00093 13 208733 120213 200293 fe5214e3
  //   1900393 1e00193 10771a63 213 b00113 f00093 13 13 208733 120213 200293 fe5212e3 1a00393 1f00193
  //   e771263 213 b00113 13 d00093 208733 120213 200293 fe5214e3 1800393 2000193 a771c63 213 b00113 13
  //   e00093 13 208733 120213 200293 fe5212e3 1900393 2100193 8771463 213 b00113 13 13 f00093 208733
  //   120213 200293 fe5212e3 1a00393 2200193 4771c63 f00093 100133 f00393 2300193 4711263 2000093 8133
  //   2000393 2400193 2711863 b3 393 2500193 2709063 1000093 1e00113 208033 393 2600193 701463 301863
  //   deade537 ead50513 dead10cc c10537 fee50513 dead10cc c0001073
  //   输出引脚
  //   状态元件的触发条件都设置成上升沿触发，时钟输入信号通过反相器输入。
  //   程序执行周期数
endmodule

module Branch (
  input  [2:0] Branch,
  input  Zero,
  input  Result0,
  output NxtASrc,
  output NxtBSrc
);

  wire not_1_out, or_1_out;

  Comparator #(.width(3), .mode("unsigned")) comparator_1 (.a(Branch), .b(3'b010), .eq(NxtASrc));  // open: gt, lt
  Multiplexer #(.select(3), .enable("false")) multiplexer_1 (
    .in0(1'b0), .in1(1'b1), .in2(1'b1), .in4(Zero), .in5(not_1_out), .in6(Result0), .in7(or_1_out),
    .out(NxtBSrc), .sel(Branch));  // open: in3
  not not_1 (not_1_out, Zero);
  or or_1 (or_1_out, Zero, ~Result0);  // OR_Gate

  // Notes on the sheet:
  //   Zero: pull=down
  //   Branch: pull=down
  //   输入信号
  //   请勿修改引脚名称、电路名称及电路封装外观
  //   不要修改控制信号的编码定义、引脚名称和在布局中的位置。
  //   输出信号
endmodule

module IFU (
  input  [31:0] Initial_Address,
  input  [31:0] Imm,
  input  [31:0] BusA,
  input  CLK,
  input  Reset,
  input  halt,
  input  NxtASrc,
  input  NxtBSrc,
  output [31:0] PC
);

  wire not_1_out;
  wire [31:0] adder_1_out, multiplexer_1_out, multiplexer_2_out, multiplexer_3_out;

  Multiplexer #(.width(32), .enable("false")) multiplexer_1 (
    .in0(adder_1_out), .in1(Initial_Address), .out(multiplexer_1_out), .sel(Reset));
  Register #(.width(32), .Select("high")) register_1 (
    .D(multiplexer_1_out), .en(not_1_out), .Q(PC), .clk(CLK), .cs(1'b1));  // open: clr, preset
  not not_1 (not_1_out, halt);
  Multiplexer #(.width(32), .enable("false")) multiplexer_2 (
    .in0(PC), .in1(BusA), .out(multiplexer_2_out), .sel(NxtASrc));
  Multiplexer #(.width(32), .enable("false")) multiplexer_3 (
    .in0(32'h4), .in1(Imm), .out(multiplexer_3_out), .sel(NxtBSrc));
  Adder #(.width(32)) adder_1 (.a(multiplexer_2_out), .b(multiplexer_3_out), .out(adder_1_out));  // open: cin, cout

  // Other names for the same wires on the sheet: Init_Addr[31:0] = Initial_Address

  // Notes on the sheet:
  //   Imm: pull=down
  //   NxtBSrc: pull=down
  //   NxtASrc: pull=down
  //   BusA: pull=down
  //   输入信号
  //   请勿修改引脚名称、电路名称及电路封装外观
  //   指令存储器256KB，数据位为32位，地址位为16位。PC寄存器数据宽度32位，片选信号高电平有效
  //   输出信号
endmodule

module \控制器  (
  input  [6:0] opcode,
  input  [2:0] funct3,
  input  [6:0] funct7,
  output [2:0] ExtOp,
  output RegWr,
  output [2:0] Branch,
  output ALUASrc,
  output [1:0] ALUBSrc,
  output [3:0] ALUctr,
  output MemtoReg,
  output [2:0] MemOp,
  output MemWr,
  output Halt
);

  wire add, addi, \and , andi, auipc, B_out, beq, bge, bgeu, blt, bltu, bne, comparator_1_eq,
       comparator_2_eq, comparator_3_eq, comparator_4_eq, comparator_5_eq, comparator_7_eq, comparator_8_eq,
       comparator_9_eq, comparator_10_eq, comparator_11_eq, comparator_12_eq, comparator_13_eq,
       comparator_14_eq, I0_out, I1_out, I2_out, jalr, lb, lbu, lh, lhu, lui, lw, \or , or_1_out, or_2_out,
       or_4_out, or_5_out, or_6_out, or_14_out, or_16_out, or_19_out, or_20_out, or_25_out, or_28_out,
       or_30_out, ori, R_out, S_out, sb, sh, sll, slli, slt, slti, sltiu, sltu, sra, srai, srl, srli, sub,
       sw, \xor , xori;

  and U0 (lui, ~opcode[6], opcode[5], opcode[4], ~opcode[3], opcode[2], opcode[1], opcode[0]);  // AND_Gate
  and U1 (auipc, ~opcode[6], ~opcode[5], opcode[4], ~opcode[3], opcode[2], opcode[1], opcode[0]);  // AND_Gate
  and I0 (I0_out, ~opcode[6], ~opcode[5], opcode[4], ~opcode[3], ~opcode[2], opcode[1], opcode[0]);  // AND_Gate
  and I1 (I1_out, opcode[6], opcode[5], ~opcode[4], ~opcode[3], opcode[2], opcode[1], opcode[0]);  // AND_Gate
  and I2 (I2_out, ~opcode[6], ~opcode[5], ~opcode[4], ~opcode[3], ~opcode[2], opcode[1], opcode[0]);  // AND_Gate
  and J (ExtOp[2], opcode[6], opcode[5], ~opcode[4], opcode[3], opcode[2], opcode[1], opcode[0]);  // AND_Gate
  and R (R_out, ~opcode[6], opcode[5], opcode[4], ~opcode[3], ~opcode[2], opcode[1], opcode[0]);  // AND_Gate
  and B (B_out, opcode[6], opcode[5], ~opcode[4], ~opcode[3], ~opcode[2], opcode[1], opcode[0]);  // AND_Gate
  and S (S_out, ~opcode[6], opcode[5], ~opcode[4], ~opcode[3], ~opcode[2], opcode[1], opcode[0]);  // AND_Gate
  or or_1 (or_1_out, bne, blt, bge, bltu, bgeu);
  or or_2 (or_2_out, lui, auipc, beq);
  or or_3 (ExtOp[0], or_2_out, or_1_out);
  or or_4 (or_4_out, beq, bne, blt);
  or or_5 (or_5_out, bge, bltu, bgeu);
  or or_6 (or_6_out, sb, sh, sw);
  or or_7 (ExtOp[1], or_4_out, or_5_out, or_6_out);
  or or_8 (ALUASrc, auipc, ExtOp[2], jalr);
  Comparator #(.width(3), .mode("unsigned")) comparator_1 (
    .a(funct3), .b(3'b000), .eq(comparator_1_eq));  // open: gt, lt
  and and_1 (jalr, I1_out, comparator_1_eq);
  and and_2 (lb, I2_out, comparator_1_eq);
  or or_9 (ALUBSrc[0], ExtOp[2], jalr);
  Comparator #(.width(1), .mode("unsigned")) comparator_2 (
    .a(funct7[5]), .b(1'b0), .eq(comparator_2_eq));  // open: gt, lt
  and and_3 (addi, I0_out, comparator_1_eq);
  or or_10 (ALUBSrc[1], lui, auipc, addi, slti, sltiu, xori, ori, andi, slli, srli, srai, lb, lh, lw, lbu, lhu, sb, sh, sw);
  and and_4 (add, R_out, comparator_1_eq, comparator_2_eq);
  and and_5 (slti, I0_out, comparator_3_eq);
  Comparator #(.width(3), .mode("unsigned")) comparator_3 (
    .a(funct3), .b(3'b010), .eq(comparator_3_eq));  // open: gt, lt
  and and_6 (lw, I2_out, comparator_3_eq);
  and and_7 (beq, B_out, comparator_1_eq);
  and and_8 (sb, S_out, comparator_1_eq);
  or or_11 (ALUctr[0], lui, sltiu, andi, slli, srli, srai, sll, sltu, srl, sra, \and , bltu, bgeu);
  Comparator #(.width(1), .mode("unsigned")) comparator_4 (
    .a(funct7[5]), .b(1'b1), .eq(comparator_4_eq));  // open: gt, lt
  and and_9 (slt, R_out, comparator_3_eq, comparator_2_eq);
  and and_10 (sltiu, I0_out, comparator_5_eq);
  Comparator #(.width(3), .mode("unsigned")) comparator_5 (
    .a(funct3), .b(3'b011), .eq(comparator_5_eq));  // open: gt, lt
  and and_11 (sw, S_out, comparator_3_eq);
  or or_12 (ALUctr[1], lui, slti, sltiu, ori, andi, slt, sltu, \or , \and , beq, bne, blt, bge, bltu, bgeu);
  Comparator #(.width(7), .mode("unsigned")) comparator_6 (.a(opcode), .b(7'b1110011), .eq(Halt));  // open: gt, lt
  and and_12 (sub, R_out, comparator_1_eq, comparator_4_eq);
  Comparator #(.width(3), .mode("unsigned")) comparator_7 (
    .a(funct3), .b(3'b100), .eq(comparator_7_eq));  // open: gt, lt
  and and_13 (sltu, R_out, comparator_5_eq, comparator_2_eq);
  or or_13 (ALUctr[2], lui, xori, ori, andi, srli, srai, \xor , srl, sra, \or , \and );
  and and_14 (xori, I0_out, comparator_7_eq);
  and and_15 (lbu, I2_out, comparator_7_eq);
  or or_14 (or_14_out, lui, srai, sub);
  or or_15 (ALUctr[3], or_14_out, sra);
  Comparator #(.width(3), .mode("unsigned")) comparator_8 (
    .a(funct3), .b(3'b110), .eq(comparator_8_eq));  // open: gt, lt
  and and_16 (\xor , R_out, comparator_7_eq, comparator_2_eq);
  and and_17 (blt, comparator_7_eq, B_out);
  or or_16 (or_16_out, ExtOp[2], bne, bge);
  or or_17 (Branch[0], or_16_out, bgeu);
  or or_18 (Branch[1], jalr, blt, bge, bltu, bgeu);
  and and_18 (ori, I0_out, comparator_8_eq);
  and and_19 (\or , R_out, comparator_8_eq, comparator_2_eq);
  and and_20 (bltu, comparator_8_eq, B_out);
  or or_19 (or_19_out, beq, bne, blt);
  or or_20 (or_20_out, bge, bltu, bgeu);
  or or_21 (Branch[2], or_19_out, or_20_out);
  Comparator #(.width(3), .mode("unsigned")) comparator_9 (
    .a(funct3), .b(3'b111), .eq(comparator_9_eq));  // open: gt, lt
  or or_22 (MemtoReg, lb, lh, lw, lbu, lhu);
  and and_21 (andi, I0_out, comparator_9_eq);
  and and_22 (\and , comparator_9_eq, R_out, comparator_2_eq);
  and and_23 (bgeu, comparator_9_eq, B_out);
  or or_23 (MemOp[0], lb, lbu, sb);
  or or_24 (MemWr, sb, sh, sw);
  Comparator #(.width(1), .mode("unsigned")) comparator_10 (
    .a(funct7[5]), .b(1'b0), .eq(comparator_10_eq));  // open: gt, lt
  Comparator #(.width(3), .mode("unsigned")) comparator_11 (
    .a(funct3), .b(3'b001), .eq(comparator_11_eq));  // open: gt, lt
  or or_25 (or_25_out, lb, lh, sb);
  or or_26 (MemOp[1], lh, lhu, sh);
  or or_27 (MemOp[2], or_25_out, sh);
  and and_24 (slli, I0_out, comparator_10_eq, comparator_11_eq);
  and and_25 (lh, comparator_11_eq, I2_out);
  and and_26 (sll, R_out, comparator_11_eq, comparator_2_eq);
  or or_28 (or_28_out, lui, auipc, addi, slti, sltiu, xori, ori, andi, slli, srli, srai, add, sub);
  and and_27 (bne, B_out, comparator_11_eq);
  and and_28 (sh, S_out, comparator_11_eq);
  or or_29 (RegWr, or_28_out, or_30_out);
  Comparator #(.width(3), .mode("unsigned")) comparator_12 (
    .a(funct3), .b(3'b101), .eq(comparator_12_eq));  // open: gt, lt
  and and_29 (lhu, I2_out, comparator_12_eq);
  or or_30 (or_30_out, sll, slt, sltu, \xor , srl, sra, \or , \and , ExtOp[2], jalr, lb, lh, lw, lbu, lhu);
  and and_30 (srli, I0_out, comparator_10_eq, comparator_12_eq);
  and and_31 (bge, B_out, comparator_12_eq);
  Comparator #(.width(1), .mode("unsigned")) comparator_13 (
    .a(funct7[5]), .b(1'b1), .eq(comparator_13_eq));  // open: gt, lt
  Comparator #(.width(3), .mode("unsigned")) comparator_14 (
    .a(funct3), .b(3'b101), .eq(comparator_14_eq));  // open: gt, lt
  and and_32 (srl, R_out, comparator_12_eq, comparator_2_eq);
  and and_33 (sra, R_out, comparator_12_eq, comparator_4_eq);
  and and_34 (srai, I0_out, comparator_13_eq, comparator_14_eq);

  // Other names for the same wires on the sheet: jal = ExtOp[2]

  // Notes on the sheet:
  //   输入引脚
  //   请勿修改引脚名称、电路名称及电路封装外观
  //   提示：根据指令种类，把7位指令code用一位指令类型标志位来表示，再通过功能码来区分具体指令，生成控制信号。
  //   输出引脚
endmodule

module IDU (
  input  [31:0] IR,
  input  [31:0] BusW,
  input  [31:0] PC,
  input  [2:0] ExtOp,
  input  RegWr,
  input  ALUASrc,
  input  [1:0] ALUBSrc,
  input  CLK,
  output [31:0] DataA,
  output [31:0] DataB,
  output [31:0] BusA,
  output [31:0] BusB,
  output [6:0] OpCode,
  output [31:0] Imm,
  output [2:0] Funct3,
  output [6:0] Funct7
);

  \立即数扩展器  \u_立即数扩展器_1  (.Instr(IR), .Extop(ExtOp), .imm(Imm));
  RegFile regfile_1 (
    .R1_num(IR[19:15]), .R2_num(IR[24:20]), .Write_Reg_num(IR[11:7]), .Write_Enable(RegWr), .Clock(CLK),
    .Din(BusW), .Reg1Out(BusA), .Reg2Out(BusB));
  Multiplexer #(.width(32), .enable("false")) multiplexer_1 (.in0(BusA), .in1(PC), .out(DataA), .sel(ALUASrc));
  Multiplexer #(.select(2), .width(32), .enable("false")) multiplexer_2 (
    .in0(BusB), .in1(32'h4), .in2(Imm), .out(DataB), .sel(ALUBSrc));  // open: in3

  assign Funct3 = IR[14:12];
  assign Funct7 = IR[31:25];
  assign OpCode = IR[6:0];

  // Other names for the same wires on the sheet: op[6:0] = IR[6:0]

  // Notes on the sheet:
  //   PC: pull=down
  //   RegWr: pull=down
  //   ExtOp: pull=down
  //   ALUBSrc: pull=down
  //   ALUASrc: pull=down
  //   BusW: pull=down
  //   输入信号
  //   为了后续实验中的引用，不要修改ALUASrc、ALUBSrc和EXtOP编码定义。
  //   请勿修改引脚名称、电路名称及电路封装外观
  //   输出信号
  //   修改寄存器堆电路设计，0号寄存器始终为0。
endmodule

module RegFile (
  input  [4:0] R1_num,
  input  [4:0] R2_num,
  input  [4:0] Write_Reg_num,
  input  [31:0] Din,
  input  Write_Enable,
  input  Clock,
  output [31:0] Reg1Out,
  output [31:0] Reg2Out
);

  wire and_1_out, and_2_out, and_3_out, and_4_out, and_5_out, and_6_out, and_7_out, and_8_out, and_9_out,
       and_10_out, and_11_out, and_12_out, and_13_out, and_14_out, and_15_out, and_16_out, and_17_out,
       and_18_out, and_19_out, and_20_out, and_21_out, and_22_out, and_23_out, and_24_out, and_25_out,
       and_26_out, and_27_out, and_28_out, and_29_out, and_30_out, and_31_out, and_32_out, decoder_1_out0,
       decoder_1_out1, decoder_1_out2, decoder_1_out3, decoder_1_out4, decoder_1_out5, decoder_1_out6,
       decoder_1_out7, decoder_1_out8, decoder_1_out9, decoder_1_out10, decoder_1_out11, decoder_1_out12,
       decoder_1_out13, decoder_1_out14, decoder_1_out15, decoder_1_out16, decoder_1_out17, decoder_1_out18,
       decoder_1_out19, decoder_1_out20, decoder_1_out21, decoder_1_out22, decoder_1_out23, decoder_1_out24,
       decoder_1_out25, decoder_1_out26, decoder_1_out27, decoder_1_out28, decoder_1_out29, decoder_1_out30,
       decoder_1_out31;
  wire [31:0] _0_q, _1_q, _2_q, _3_q, _4_q, _5_q, _6_q, _7_q, _8_q, _9_q, register_1_q, register_2_q,
       register_3_q, register_4_q, register_5_q, register_6_q, register_7_q, register_8_q, register_9_q,
       register_10_q, register_11_q, register_12_q, register_13_q, register_14_q, register_15_q,
       register_16_q, register_17_q, register_18_q, register_19_q, register_20_q, register_21_q,
       register_22_q;

  Decoder #(.select(5), .enable("false")) decoder_1 (
    .out0(decoder_1_out0), .out1(decoder_1_out1), .out2(decoder_1_out2), .out3(decoder_1_out3),
    .out4(decoder_1_out4), .out5(decoder_1_out5), .out6(decoder_1_out6), .out7(decoder_1_out7),
    .out8(decoder_1_out8), .out9(decoder_1_out9), .out10(decoder_1_out10), .out11(decoder_1_out11),
    .out12(decoder_1_out12), .out13(decoder_1_out13), .out14(decoder_1_out14), .out15(decoder_1_out15),
    .out16(decoder_1_out16), .out17(decoder_1_out17), .out18(decoder_1_out18), .out19(decoder_1_out19),
    .out20(decoder_1_out20), .out21(decoder_1_out21), .out22(decoder_1_out22), .out23(decoder_1_out23),
    .out24(decoder_1_out24), .out25(decoder_1_out25), .out26(decoder_1_out26), .out27(decoder_1_out27),
    .out28(decoder_1_out28), .out29(decoder_1_out29), .out30(decoder_1_out30), .out31(decoder_1_out31),
    .sel(Write_Reg_num));
  and and_1 (and_1_out, decoder_1_out0, Write_Enable);
  and and_2 (and_2_out, decoder_1_out1, Write_Enable);
  and and_3 (and_3_out, decoder_1_out2, Write_Enable);
  and and_4 (and_4_out, decoder_1_out3, Write_Enable);
  and and_5 (and_5_out, decoder_1_out4, Write_Enable);
  and and_6 (and_6_out, decoder_1_out5, Write_Enable);
  and and_7 (and_7_out, decoder_1_out6, Write_Enable);
  and and_8 (and_8_out, decoder_1_out7, Write_Enable);
  and and_9 (and_9_out, decoder_1_out8, Write_Enable);
  and and_10 (and_10_out, decoder_1_out9, Write_Enable);
  and and_11 (and_11_out, decoder_1_out10, Write_Enable);
  and and_12 (and_12_out, decoder_1_out11, Write_Enable);
  and and_13 (and_13_out, decoder_1_out12, Write_Enable);
  and and_14 (and_14_out, decoder_1_out13, Write_Enable);
  and and_15 (and_15_out, decoder_1_out14, Write_Enable);
  and and_16 (and_16_out, decoder_1_out15, Write_Enable);
  and and_17 (and_17_out, decoder_1_out16, Write_Enable);
  and and_18 (and_18_out, decoder_1_out17, Write_Enable);
  and and_19 (and_19_out, decoder_1_out18, Write_Enable);
  and and_20 (and_20_out, decoder_1_out19, Write_Enable);
  and and_21 (and_21_out, decoder_1_out20, Write_Enable);
  and and_22 (and_22_out, decoder_1_out21, Write_Enable);
  and and_23 (and_23_out, decoder_1_out22, Write_Enable);
  and and_24 (and_24_out, decoder_1_out23, Write_Enable);
  and and_25 (and_25_out, decoder_1_out24, Write_Enable);
  and and_26 (and_26_out, decoder_1_out25, Write_Enable);
  and and_27 (and_27_out, decoder_1_out26, Write_Enable);
  and and_28 (and_28_out, decoder_1_out27, Write_Enable);
  and and_29 (and_29_out, decoder_1_out28, Write_Enable);
  and and_30 (and_30_out, decoder_1_out29, Write_Enable);
  and and_31 (and_31_out, decoder_1_out30, Write_Enable);
  and and_32 (and_32_out, decoder_1_out31, Write_Enable);
  Register #(.width(32), .Select("low")) _0 (.D({32{1'b0}}), .en(and_1_out), .Q(_0_q), .clk(Clock));  // open: clr
  Register #(.width(32), .Select("low")) _1 (.D(Din), .en(and_2_out), .Q(_1_q), .clk(Clock));  // open: clr
  Register #(.width(32), .Select("low")) _2 (.D(Din), .en(and_3_out), .Q(_2_q), .clk(Clock));  // open: clr
  Register #(.width(32), .Select("low")) _3 (.D(Din), .en(and_4_out), .Q(_3_q), .clk(Clock));  // open: clr
  Register #(.width(32), .Select("low")) _4 (.D(Din), .en(and_5_out), .Q(_4_q), .clk(Clock));  // open: clr
  Register #(.width(32), .Select("low")) _5 (.D(Din), .en(and_6_out), .Q(_5_q), .clk(Clock));  // open: clr
  Register #(.width(32), .Select("low")) _6 (.D(Din), .en(and_7_out), .Q(_6_q), .clk(Clock));  // open: clr
  Register #(.width(32), .Select("low")) _7 (.D(Din), .en(and_8_out), .Q(_7_q), .clk(Clock));  // open: clr
  Register #(.width(32), .Select("low")) _8 (.D(Din), .en(and_9_out), .Q(_8_q), .clk(Clock));  // open: clr
  Register #(.width(32), .Select("low")) _9 (.D(Din), .en(and_10_out), .Q(_9_q), .clk(Clock));  // open: clr
  Register #(.width(32), .Select("low")) register_1 (
    .D(Din), .en(and_11_out), .Q(register_1_q), .clk(Clock));  // open: clr
  Register #(.width(32), .Select("low")) register_2 (
    .D(Din), .en(and_12_out), .Q(register_2_q), .clk(Clock));  // open: clr
  Register #(.width(32), .Select("low")) register_3 (
    .D(Din), .en(and_13_out), .Q(register_3_q), .clk(Clock));  // open: clr
  Register #(.width(32), .Select("low")) register_4 (
    .D(Din), .en(and_14_out), .Q(register_4_q), .clk(Clock));  // open: clr
  Register #(.width(32), .Select("low")) register_5 (
    .D(Din), .en(and_15_out), .Q(register_5_q), .clk(Clock));  // open: clr
  Register #(.width(32), .Select("low")) register_6 (
    .D(Din), .en(and_16_out), .Q(register_6_q), .clk(Clock));  // open: clr
  Register #(.width(32), .Select("low")) register_7 (
    .D(Din), .en(and_17_out), .Q(register_7_q), .clk(Clock));  // open: clr
  Register #(.width(32), .Select("low")) register_8 (
    .D(Din), .en(and_18_out), .Q(register_8_q), .clk(Clock));  // open: clr
  Register #(.width(32), .Select("low")) register_9 (
    .D(Din), .en(and_19_out), .Q(register_9_q), .clk(Clock));  // open: clr
  Register #(.width(32), .Select("low")) register_10 (
    .D(Din), .en(and_20_out), .Q(register_10_q), .clk(Clock));  // open: clr
  Register #(.width(32), .Select("low")) register_11 (
    .D(Din), .en(and_21_out), .Q(register_11_q), .clk(Clock));  // open: clr
  Register #(.width(32), .Select("low")) register_12 (
    .D(Din), .en(and_22_out), .Q(register_12_q), .clk(Clock));  // open: clr
  Register #(.width(32), .Select("low")) register_13 (
    .D(Din), .en(and_23_out), .Q(register_13_q), .clk(Clock));  // open: clr
  Register #(.width(32), .Select("low")) register_14 (
    .D(Din), .en(and_24_out), .Q(register_14_q), .clk(Clock));  // open: clr
  Register #(.width(32), .Select("low")) register_15 (
    .D(Din), .en(and_25_out), .Q(register_15_q), .clk(Clock));  // open: clr
  Register #(.width(32), .Select("low")) register_16 (
    .D(Din), .en(and_26_out), .Q(register_16_q), .clk(Clock));  // open: clr
  Register #(.width(32), .Select("low")) register_17 (
    .D(Din), .en(and_27_out), .Q(register_17_q), .clk(Clock));  // open: clr
  Register #(.width(32), .Select("low")) register_18 (
    .D(Din), .en(and_28_out), .Q(register_18_q), .clk(Clock));  // open: clr
  Register #(.width(32), .Select("low")) register_19 (
    .D(Din), .en(and_29_out), .Q(register_19_q), .clk(Clock));  // open: clr
  Register #(.width(32), .Select("low")) register_20 (
    .D(Din), .en(and_30_out), .Q(register_20_q), .clk(Clock));  // open: clr
  Register #(.width(32), .Select("low")) register_21 (
    .D(Din), .en(and_31_out), .Q(register_21_q), .clk(Clock));  // open: clr
  Register #(.width(32), .Select("low")) register_22 (.D(Din), .en(and_32_out), .Q(register_22_q));  // open: clk, clr
  Multiplexer #(.select(5), .width(32), .enable("false")) multiplexer_1 (
    .in0(_0_q), .in1(_1_q), .in2(_2_q), .in3(_3_q), .in4(_4_q), .in5(_5_q), .in6(_6_q), .in7(_7_q),
    .in8(_8_q), .in9(_9_q), .in10(register_1_q), .in11(register_2_q), .in12(register_3_q),
    .in13(register_4_q), .in14(register_5_q), .in15(register_6_q), .in16(register_7_q), .in17(register_8_q),
    .in18(register_9_q), .in19(register_10_q), .in20(register_11_q), .in21(register_12_q),
    .in22(register_13_q), .in23(register_14_q), .in24(register_15_q), .in25(register_16_q),
    .in26(register_17_q), .in27(register_18_q), .in28(register_19_q), .in29(register_20_q),
    .in30(register_21_q), .in31(register_22_q), .out(Reg1Out), .sel(R1_num));
  Multiplexer #(.select(5), .width(32), .enable("false")) multiplexer_2 (
    .in0(_0_q), .in1(_1_q), .in2(_2_q), .in3(_3_q), .in4(_4_q), .in5(_5_q), .in6(_6_q), .in7(_7_q),
    .in8(_8_q), .in9(_9_q), .in10(register_1_q), .in11(register_2_q), .in12(register_3_q),
    .in13(register_4_q), .in14(register_5_q), .in15(register_6_q), .in16(register_7_q), .in17(register_8_q),
    .in18(register_9_q), .in19(register_10_q), .in20(register_11_q), .in21(register_12_q),
    .in22(register_13_q), .in23(register_14_q), .in24(register_15_q), .in25(register_16_q),
    .in26(register_17_q), .in27(register_18_q), .in28(register_19_q), .in29(register_20_q),
    .in30(register_21_q), .in31(register_22_q), .out(Reg2Out), .sel(R2_num));

  // Other names for the same wires on the sheet: CLK = Clock; RA[4:0] = R1_num; RB[4:0] = R2_num; RDA[31:0] = Reg1Out;
  //   RDB[31:0] = Reg2Out; RW[4:0] = Write_Reg_num; WE = Write_Enable

  // Notes on the sheet:
  //   输入引脚
  //   请勿修改引脚名称、电路名称及电路封装外观
  //   提示：使用译码器、多路选择器和32位寄存器及逻辑门实现寄存器堆，禁止直接使用存储器组件。
  //   提示：使用译码器、多路选择器和32位寄存器及逻辑门实现寄存器堆，禁止直接使用存储器组件。
  //   输出引脚
endmodule

module \立即数扩展器  (
  input  [31:0] Instr,
  input  [2:0] Extop,
  output [31:0] imm
);

  wire [11:0] bit_extender_4_out;
  wire [19:0] bit_extender_3_out;
  wire [20:0] bit_extender_1_out, bit_extender_2_out;

  assign bit_extender_1_out = {{20{Instr[31]}}, Instr[31]};  // Bit_Extender bit_extender_1
  assign bit_extender_2_out = {{20{Instr[31]}}, Instr[31]};  // Bit_Extender bit_extender_2
  assign bit_extender_3_out = {{19{Instr[31]}}, Instr[31]};  // Bit_Extender bit_extender_3
  assign bit_extender_4_out = {{11{Instr[31]}}, Instr[31]};  // Bit_Extender bit_extender_4
  Multiplexer #(.select(3), .width(32), .enable("false")) multiplexer_1 (
    .in0({bit_extender_1_out, Instr[30:20]}), .in1({Instr[31:12], {12{1'b0}}}),
    .in2({bit_extender_2_out, Instr[30:25], Instr[11:7]}),
    .in3({bit_extender_3_out, Instr[7], Instr[30:25], Instr[11:8], 1'b0}),
    .in4({bit_extender_4_out, Instr[19:12], Instr[20], Instr[30:21], 1'b0}), .out(imm), .sel(Extop));  // open: in5, in6, in7

  // Notes on the sheet:
  //   Instr: pull=down
  //   Extop: pull=down
  //   输入引脚
  //   输出引脚
endmodule

module DataRAM (
  input  CLK,
  input  CLR,
  input  WE,
  input  [2:0] MemOp,
  input  [17:0] Addr,
  input  [31:0] Din,
  output AlignErr,
  output [31:0] DataOut
);

  wire and_1_out, SEL0, SEL1, SEL2, SEL3;
  wire [7:0] multiplexer_3_out, multiplexer_4_out, multiplexer_5_out, multiplexer_6_out, ram_1_data,
       ram_2_data, ram_3_data, ram_4_data;
  wire [15:0] multiplexer_7_out;
  wire [17:0] multiplexer_2_out;
  wire [31:0] bit_extender_1_out, bit_extender_2_out, bit_extender_3_out, bit_extender_4_out,
       multiplexer_1_out, multiplexer_8_out, multiplexer_9_out;

  Multiplexer #(.width(32), .enable("false")) multiplexer_1 (
    .in0(Din), .out(multiplexer_1_out), .sel(AlignErr));  // open: in1
  Multiplexer #(.width(18), .enable("false")) multiplexer_2 (
    .in0(Addr), .out(multiplexer_2_out), .sel(AlignErr));  // open: in1
  Multiplexer #(.select(2), .width(8), .enable("false")) multiplexer_3 (
    .in0(multiplexer_1_out[31:24]), .in2(multiplexer_1_out[15:8]), .in3(multiplexer_1_out[7:0]),
    .out(multiplexer_3_out), .sel(Addr[1:0]));  // open: in1
  Multiplexer #(.width(8), .enable("false")) multiplexer_4 (
    .in0(multiplexer_1_out[23:16]), .in1(multiplexer_1_out[7:0]), .out(multiplexer_4_out), .sel(Addr[1]));
  Multiplexer #(.width(8), .enable("false")) multiplexer_5 (
    .in0(multiplexer_1_out[15:8]), .in1(multiplexer_1_out[7:0]), .out(multiplexer_5_out), .sel(Addr[0]));
  RAM #(.addrWidth(16), .bus("separate"), .Select("high")) ram_1 (
    .addr(multiplexer_2_out[17:2]), .din(multiplexer_3_out), .data(ram_1_data), .str(WE), .sel(SEL3),
    .clk(CLK), .clr(CLR));  // open: ld
  RAM #(.addrWidth(16), .bus("separate"), .Select("high")) ram_2 (
    .addr(multiplexer_2_out[17:2]), .din(multiplexer_4_out), .data(ram_2_data), .str(WE), .sel(SEL2),
    .clk(CLK), .clr(CLR));  // open: ld
  RAM #(.addrWidth(16), .bus("separate"), .Select("high")) ram_3 (
    .addr(multiplexer_2_out[17:2]), .din(multiplexer_5_out), .data(ram_3_data), .str(WE), .sel(SEL1),
    .clk(CLK), .clr(CLR));  // open: ld
  RAM #(.addrWidth(16), .bus("separate"), .Select("high")) ram_4 (
    .addr(multiplexer_2_out[17:2]), .din(multiplexer_1_out[7:0]), .data(ram_4_data), .str(WE), .sel(SEL0),
    .clk(CLK), .clr(CLR));  // open: ld
  Multiplexer #(.select(2), .width(8), .enable("false")) multiplexer_6 (
    .in0(ram_4_data), .in1(ram_3_data), .in2(ram_2_data), .in3(ram_1_data), .out(multiplexer_6_out),
    .sel(Addr[1:0]));
  Multiplexer #(.width(16), .enable("false")) multiplexer_7 (
    .in0({ram_3_data, ram_4_data}), .in1({ram_1_data, ram_2_data}), .out(multiplexer_7_out), .sel(Addr[1]));
  assign bit_extender_1_out = {{24{1'b0}}, multiplexer_6_out};  // Bit_Extender bit_extender_1
  Multiplexer #(.width(32), .enable("false")) multiplexer_8 (
    .in0(bit_extender_1_out), .in1(bit_extender_2_out), .out(multiplexer_8_out), .sel(MemOp[2]));
  assign bit_extender_2_out = {{24{multiplexer_6_out[7]}}, multiplexer_6_out};  // Bit_Extender bit_extender_2
  assign bit_extender_3_out = {{16{1'b0}}, multiplexer_7_out};  // Bit_Extender bit_extender_3
  Multiplexer #(.width(32), .enable("false")) multiplexer_9 (
    .in0(bit_extender_3_out), .in1(bit_extender_4_out), .out(multiplexer_9_out), .sel(MemOp[2]));
  assign bit_extender_4_out = {{16{multiplexer_7_out[15]}}, multiplexer_7_out};  // Bit_Extender bit_extender_4
  Multiplexer #(.select(2), .width(32), .enable("false")) multiplexer_10 (
    .in0({ram_1_data, ram_2_data, ram_3_data, ram_4_data}), .in1(multiplexer_8_out), .in2(multiplexer_9_out),
    .out(DataOut), .sel(MemOp[1:0]));  // open: in3
  Sel sel_1 (.in_1(MemOp), .out_4(SEL0), .out_5(SEL1), .in_2(Addr[0]), .out_6(SEL2), .in_3(Addr[1]), .out_7(SEL3));
  and and_1 (and_1_out, ~SEL0, ~SEL1, ~SEL2, ~SEL3);  // AND_Gate
  Err err_1 (.in_1(MemOp), .in_2(and_1_out), .out_3(AlignErr));

  // Other names for the same wires on the sheet: Dout[31:0] = DataOut

  // Notes on the sheet:
  //   输入引脚
  //   请勿修改引脚名称、电路名称及电路封装外观
  //   输出引脚
endmodule

module ALU (
  input  [3:0] ALUctr,
  input  [31:0] A,
  input  [31:0] B,
  output Zero,
  output [31:0] S
);

  wire adder32_1_cf, adder32_1_of, adder32_1_sf, aluctrl_1_alctr, aluctrl_1_sftctr, aluctrl_1_sigctr,
       aluctrl_1_subctr, multiplexer_1_out, xor_3_out;
  wire [2:0] aluctrl_1_opctr;
  wire [31:0] adder32_1_s, and_1_out, bit_extender_1_out, bit_extender_2_out, or_1_out, shifter32_1_dataout,
       xor_1_out, xor_2_out;

  assign bit_extender_1_out = {{31{aluctrl_1_subctr}}, aluctrl_1_subctr};  // Bit_Extender bit_extender_1
  Adder32 adder32_1 (
    .CF(adder32_1_cf), .OF(adder32_1_of), .SF(adder32_1_sf), .ZF(Zero), .X(A), .Y(xor_1_out),
    .Cin(aluctrl_1_subctr), .S(adder32_1_s));  // open: Cout
  assign xor_1_out = bit_extender_1_out ^ B;  // XOR_Gate xor_1, 32 bits wide
  assign and_1_out = A & B;  // AND_Gate and_1, 32 bits wide
  assign or_1_out = A | B;  // OR_Gate or_1, 32 bits wide
  assign xor_2_out = A ^ B;  // XOR_Gate xor_2, 32 bits wide
  Shifter32 shifter32_1 (
    .DataIn(A), .shamt(B[4:0]), .L_R(aluctrl_1_sftctr), .A_L(aluctrl_1_alctr), .DataOut(shifter32_1_dataout));
  ALUctrl aluctrl_1 (
    .SUBctr(aluctrl_1_subctr), .SFTctr(aluctrl_1_sftctr), .SIGctr(aluctrl_1_sigctr), .ALctr(aluctrl_1_alctr),
    .OPctr(aluctrl_1_opctr), .ALUctr(ALUctr));
  xor xor_3 (xor_3_out, adder32_1_of, adder32_1_sf);
  Multiplexer #(.enable("false")) multiplexer_1 (
    .in0(adder32_1_cf), .in1(xor_3_out), .out(multiplexer_1_out), .sel(aluctrl_1_sigctr));
  Multiplexer #(.select(3), .width(32), .enable("false")) multiplexer_2 (
    .in0(adder32_1_s), .in1(and_1_out), .in2(or_1_out), .in3(xor_2_out), .in4(shifter32_1_dataout), .in5(B),
    .in6(bit_extender_2_out), .out(S), .sel(aluctrl_1_opctr));  // open: in7
  // Probe on A
  // Probe on B
  // Probe on S
  assign bit_extender_2_out = {{31{1'b0}}, multiplexer_1_out};  // Bit_Extender bit_extender_2

  // Other names for the same wires on the sheet: Result[31:0] = S

  // Notes on the sheet:
  //   ALUctr: pull=down
  //   B: pull=down
  //   A: pull=down
  //   输入引脚
  //   请勿修改引脚名称、电路名称及电路封装外观
  //   提示：使用32位并行加法器子电路、桶形移位器、ALU控制子电路实现32位ALU
  //   功能说明:32位ALU，输入32位操作数A、B，4位控制信号ALUctr，输出32位结果Reseult和1位Zero标志位
  //   输出引脚
  //   操作数和结果
endmodule

module ALUctrl (
  input  [3:0] ALUctr,
  output SUBctr,
  output SFTctr,
  output SIGctr,
  output ALctr,
  output [2:0] OPctr
);

  wire and_1_out, and_2_out, and_6_out, and_7_out, and_8_out, and_9_out, and_10_out, and_11_out, and_12_out;

  and and_1 (and_1_out, ~ALUctr[3], ~ALUctr[2], ALUctr[1]);  // AND_Gate
  and and_2 (and_2_out, ALUctr[3], ~ALUctr[2], ~ALUctr[1], ~ALUctr[0]);  // AND_Gate
  or or_1 (SUBctr, and_1_out, and_2_out);
  and and_3 (SIGctr, ~ALUctr[3], ~ALUctr[2], ALUctr[1], ~ALUctr[0]);  // AND_Gate
  and and_4 (ALctr, ALUctr[3], ALUctr[2], ~ALUctr[1], ALUctr[0]);  // AND_Gate
  and and_5 (SFTctr, ~ALUctr[3], ~ALUctr[2], ~ALUctr[1], ALUctr[0]);  // AND_Gate
  and and_6 (and_6_out, ~ALUctr[3], ~ALUctr[2], ALUctr[1]);  // AND_Gate
  and and_7 (and_7_out, ~ALUctr[3], ~ALUctr[1], ALUctr[0]);  // AND_Gate
  and and_8 (and_8_out, ALUctr[3], ALUctr[2], ALUctr[0]);
  and and_9 (and_9_out, ~ALUctr[3], ~ALUctr[2], ALUctr[1]);  // AND_Gate
  and and_10 (and_10_out, ~ALUctr[3], ALUctr[2], ~ALUctr[0]);  // AND_Gate
  and and_11 (and_11_out, ~ALUctr[3], ALUctr[2], ~ALUctr[1], ~ALUctr[0]);  // AND_Gate
  and and_12 (and_12_out, ALUctr[2], ALUctr[1], ALUctr[0]);
  or or_2 (OPctr[2], and_6_out, and_7_out, and_8_out);
  or or_3 (OPctr[1], and_9_out, and_10_out);
  or or_4 (OPctr[0], and_11_out, and_12_out);

  // Other names for the same wires on the sheet: LRctr = SFTctr

  // Notes on the sheet:
  //   输入引脚
  //   ALU操作控制信号生成部件
  //   输出引脚
endmodule

module Adder32 (
  input  Cin,
  input  [31:0] X,
  input  [31:0] Y,
  output CF,
  output Cout,
  output OF,
  output SF,
  output [31:0] S,
  output ZF
);

  wire adder16_2_c16, and_1_out, and_2_out, or_1_out;

  Adder16 adder16_1 (.X(X[31:16]), .Y(Y[31:16]), .C0(adder16_2_c16), .S(S[31:16]), .C16(Cout));  // open: Pg, Gg
  xor xor_1 (CF, Cout, Cin);
  Adder16 adder16_2 (.X(X[15:0]), .Y(Y[15:0]), .C0(Cin), .S(S[15:0]), .C16(adder16_2_c16));  // open: Pg, Gg
  // Probe on X
  // Probe on Y
  // Probe on S
  and and_1 (and_1_out, ~X[31], ~Y[31], S[31]);  // AND_Gate
  and and_2 (and_2_out, X[31], Y[31], ~S[31]);  // AND_Gate
  or or_1 (or_1_out, S[0], S[1], S[2], S[3], S[4], S[5], S[6], S[7], S[8], S[9], S[10], S[11], S[12], S[13], S[14], S[15], S[17], S[18], S[19], S[20], S[21], S[22], S[23], S[24], S[25], S[26], S[27], S[28], S[29], S[30], S[31], S[16]);
  or or_2 (OF, and_1_out, and_2_out);
  not not_1 (ZF, or_1_out);

  assign SF = S[31];

  // Notes on the sheet:
  //   Y: pull=down
  //   X: pull=down
  //   Cin: pull=down
  //   输入引脚区
  //   输出引脚区
  //   请勿修改引脚名称、电路名称及电路封装外观
  //   提示：使用16位并行加法器子电路实现32位快速加法器
  //   功能说明:32位Adder  S=X+Y，Cout为最高位进位位，Cin为进位输入， S为和，溢出OF、进位CF、零ZF、符号SF。
  //   +
  //   =
  //   无符号加法
endmodule

// 移位器
module Shifter32 (
  input  [4:0] shamt,
  input  L_R,
  input  A_L,
  input  [31:0] DataIn,
  output [31:0] DataOut
);

  wire [0:0] multiplexer_2_out;
  wire [3:0] multiplexer_4_out, multiplexer_6_out;
  wire [7:0] multiplexer_7_out, multiplexer_8_out;
  wire [15:0] multiplexer_7_out_3, multiplexer_10_out;
  wire [15:8] multiplexer_7_out_2;
  wire [31:0] multiplexer_3_out, multiplexer_5_out, multiplexer_9_out;

  Multiplexer #(.enable("false")) multiplexer_1 (.in0(1'b0), .in1(DataIn[31]), .out(multiplexer_3_out[31]), .sel(A_L));
  Multiplexer #(.enable("false")) multiplexer_2 (.in0(1'b0), .in1(DataIn[31]), .out(multiplexer_2_out[0]), .sel(A_L));
  Multiplexer #(.select(2), .width(32), .enable("false")) multiplexer_3 (
    .in0(DataIn), .in1(DataIn), .in2({multiplexer_3_out[31], DataIn[31:1]}),
    .in3({DataIn[30:0], multiplexer_2_out[0]}), .out({multiplexer_3_out[29:0], multiplexer_4_out[3:2]}),
    .sel({shamt[0], L_R}));
  Multiplexer #(.width(2), .enable("false")) multiplexer_4 (
    .in0(2'b00), .in1(multiplexer_3_out[29:28]), .out(multiplexer_4_out[1:0]), .sel(A_L));
  Multiplexer #(.select(2), .width(32), .enable("false")) multiplexer_5 (
    .in0({multiplexer_3_out[29:0], multiplexer_4_out[3:2]}),
    .in1({multiplexer_3_out[29:0], multiplexer_4_out[3:2]}),
    .in2({{2{multiplexer_3_out[31]}}, multiplexer_3_out[29:0]}),
    .in3({multiplexer_3_out[27:0], multiplexer_4_out}), .out(multiplexer_5_out), .sel({shamt[1], L_R}));
  Multiplexer #(.width(4), .enable("false")) multiplexer_6 (
    .in0(4'b0000), .in1(multiplexer_5_out[31:28]), .out(multiplexer_6_out), .sel(A_L));
  Multiplexer #(.select(2), .width(32), .enable("false")) multiplexer_7 (
    .in0(multiplexer_5_out), .in1(multiplexer_5_out),
    .in2({{4{multiplexer_3_out[31]}}, multiplexer_5_out[31:4]}),
    .in3({multiplexer_5_out[27:0], multiplexer_6_out}),
    .out({multiplexer_7_out, multiplexer_7_out_3, multiplexer_7_out_2}), .sel({shamt[2], L_R}));
  Multiplexer #(.width(8), .enable("false")) multiplexer_8 (
    .in0({8{1'b0}}), .in1(multiplexer_7_out), .out(multiplexer_8_out), .sel(A_L));
  Multiplexer #(.select(2), .width(32), .enable("false")) multiplexer_9 (
    .in0({multiplexer_7_out, multiplexer_7_out_3, multiplexer_7_out_2}),
    .in1({multiplexer_7_out, multiplexer_7_out_3, multiplexer_7_out_2}),
    .in2({{8{multiplexer_3_out[31]}}, multiplexer_7_out, multiplexer_7_out_3}),
    .in3({multiplexer_7_out_3, multiplexer_7_out_2, multiplexer_8_out}), .out(multiplexer_9_out),
    .sel({shamt[3], L_R}));
  Multiplexer #(.width(16), .enable("false")) multiplexer_10 (
    .in0({16{1'b0}}), .in1(multiplexer_9_out[31:16]), .out(multiplexer_10_out), .sel(A_L));
  Multiplexer #(.select(2), .width(32), .enable("false")) multiplexer_11 (
    .in0(multiplexer_9_out), .in1(multiplexer_9_out),
    .in2({{16{multiplexer_3_out[31]}}, multiplexer_9_out[31:16]}),
    .in3({multiplexer_9_out[15:0], multiplexer_10_out}), .out(DataOut), .sel({shamt[4], L_R}));

  // Other names for the same wires on the sheet: Left_Right = L_R; Din[31:0] = DataIn; Arth_Logic = A_L;
  //   Dout[31:0] = DataOut

  // Notes on the sheet:
  //   L/R,A/L: 00逻辑右移，01算术右移，10逻辑左移，11：循环左移
  //   输入引脚
  //   请勿修改引脚名称、电路名称及电路封装外观
  //   提示：使用多路选择器、逻辑门实现32位桶形移位器，禁止直接使用移位器组件。
  //   输出引脚
endmodule

module Adder16 (
  input  C0,
  input  [15:0] X,
  input  [15:0] Y,
  output C16,
  output Pg,
  output Gg,
  output [15:0] S
);

  wire cla4_1_gg, cla4_1_pg, cla4_2_gg, cla4_2_pg, cla4_3_gg, cla4_3_pg, cla4_4_gg, cla4_4_pg, clu4_1_c1,
       clu4_1_c2, clu4_1_c3;

  CLA4 cla4_1 (
    .X(X[15:12]), .F(S[15:12]), .Y(Y[15:12]), .Pg(cla4_1_pg), .Cin(clu4_1_c3), .Gg(cla4_1_gg));  // open: Cout
  CLA4 cla4_2 (.X(X[11:8]), .F(S[11:8]), .Y(Y[11:8]), .Pg(cla4_2_pg), .Cin(clu4_1_c2), .Gg(cla4_2_gg));  // open: Cout
  CLU4 clu4_1 (
    .P0(cla4_4_pg), .P1(cla4_3_pg), .P2(cla4_2_pg), .P3(cla4_1_pg), .C1(clu4_1_c1), .C3(clu4_1_c3),
    .G0(cla4_4_gg), .G1(cla4_3_gg), .G2(cla4_2_gg), .G3(cla4_1_gg), .C2(clu4_1_c2), .C4(C16), .C0(C0),
    .Pg(Pg), .Gg(Gg));
  CLA4 cla4_3 (.X(X[7:4]), .F(S[7:4]), .Y(Y[7:4]), .Pg(cla4_3_pg), .Cin(clu4_1_c1), .Gg(cla4_3_gg));  // open: Cout
  CLA4 cla4_4 (.X(X[3:0]), .F(S[3:0]), .Y(Y[3:0]), .Pg(cla4_4_pg), .Cin(C0), .Gg(cla4_4_gg));  // open: Cout
  // Probe on X
  // Probe on Y
  // Probe on S

  // Notes on the sheet:
  //   C0: pull=down
  //   X: pull=down
  //   Y: pull=down
  //   输入引脚区
  //   请勿修改引脚名称、电路名称及电路封装外观
  //   提示：使用4位先行进位加法器和CLU子电路实现16位并行加法器
  //   功能说明:16位Adder  S=X+Y，C16为最高位进位位，C0为进位输入， Pg、Gg为成组进位生成传递函数
  //   输出引脚区
  //   +
  //   =
  //   无符号加法
endmodule

module CLA4 (
  input  [3:0] X,
  input  [3:0] Y,
  input  Cin,
  output [3:0] F,
  output Cout,
  output Pg,
  output Gg
);

  wire clu4_1_c1, clu4_1_c2, clu4_1_c3, fa_1_g, fa_1_p, fa_2_g, fa_2_p, fa_3_g, fa_3_p, fa_4_g, fa_4_p;

  Hex_Digit_Display hex_digit_display_1 (.value(X));  // open: dp
  FA fa_1 (.A(X[3]), .F(F[3]), .B(Y[3]), .P(fa_1_p), .Cin(clu4_1_c3), .G(fa_1_g));
  Hex_Digit_Display hex_digit_display_2 (.value(Y));  // open: dp
  FA fa_2 (.A(X[2]), .F(F[2]), .B(Y[2]), .P(fa_2_p), .Cin(clu4_1_c2), .G(fa_2_g));
  FA fa_3 (.A(X[1]), .F(F[1]), .B(Y[1]), .P(fa_3_p), .Cin(clu4_1_c1), .G(fa_3_g));
  Hex_Digit_Display hex_digit_display_3 (.value(F));  // open: dp
  CLU4 clu4_1 (
    .P0(fa_4_p), .P1(fa_3_p), .P2(fa_2_p), .P3(fa_1_p), .C1(clu4_1_c1), .C3(clu4_1_c3), .G0(fa_4_g),
    .G1(fa_3_g), .G2(fa_2_g), .G3(fa_1_g), .C2(clu4_1_c2), .C4(Cout), .C0(Cin), .Pg(Pg), .Gg(Gg));
  FA fa_4 (.A(X[0]), .F(F[0]), .B(Y[0]), .P(fa_4_p), .Cin(Cin), .G(fa_4_g));

  // Other names for the same wires on the sheet: Z[3:0] = F

  // Notes on the sheet:
  //   +
  //   =
  //   输出
  //   输入
  //   请勿修改引脚名称、电路名称及电路封装外观
  //   提示：使用全加器和CLU子电路实现四位先行进位加法器CLA4
endmodule

module CLU4 (
  input  P0,
  input  P1,
  input  P2,
  input  P3,
  input  G0,
  input  G1,
  input  G2,
  input  G3,
  input  C0,
  output C1,
  output C3,
  output C2,
  output C4,
  output Pg,
  output Gg
);

  wire and_2_out, and_3_out, and_4_out, and_5_out, and_6_out, and_7_out, and_8_out, and_9_out, and_10_out,
       and_11_out;

  and and_1 (Pg, P3, P2, P1, P0);
  and and_2 (and_2_out, P3, G2);
  or or_1 (C4, G3, and_2_out, and_3_out, and_4_out, and_5_out);
  and and_3 (and_3_out, P3, P2, G1);
  and and_4 (and_4_out, P3, P2, P1, G0);
  or or_2 (Gg, and_4_out, and_3_out, and_2_out, G3);
  and and_5 (and_5_out, P3, P2, P1, P0, C0);
  or or_3 (C3, G2, and_7_out, and_6_out, and_8_out);
  and and_6 (and_6_out, P2, P1, G0);
  and and_7 (and_7_out, P2, G1);
  and and_8 (and_8_out, P2, P1, P0, C0);
  or or_4 (C2, G1, and_9_out, and_10_out);
  and and_9 (and_9_out, P1, G0);
  and and_10 (and_10_out, P1, P0, C0);
  or or_5 (C1, G0, and_11_out);
  and and_11 (and_11_out, P0, C0);

  // Notes on the sheet:
  //   输入引脚
  //   请勿修改引脚名称、电路名称及电路封装外观
  //   提示：使用逻辑门电路实现4位四位先行进位部件CLU，Pg、Gg为成组进位生成传递函数
  //   输出引脚
endmodule

module FA (
  input  A,
  input  B,
  input  Cin,
  output F,
  output P,
  output G
);

  wire and_2_out, and_3_out, and_4_out, and_5_out;

  or or_1 (P, B, A);
  and and_1 (G, B, A);
  and and_2 (and_2_out, A, B, Cin);
  and and_3 (and_3_out, A, ~B, ~Cin);  // AND_Gate
  and and_4 (and_4_out, B, ~A, ~Cin);  // AND_Gate
  and and_5 (and_5_out, Cin, ~A, ~B);  // AND_Gate
  or or_2 (F, and_2_out, and_3_out, and_4_out, and_5_out);

  // Notes on the sheet:
  //   输入引脚
  //   请勿修改引脚名称、电路名称及电路封装外观
  //   输出引脚
endmodule

module Sel (
  input  [2:0] in_1,
  input  in_2,
  input  in_3,
  output out_4,
  output out_5,
  output out_6,
  output out_7
);

  wire and_1_out, and_2_out, and_3_out, and_4_out, and_5_out, and_6_out, and_7_out;

  and and_1 (and_1_out, ~in_1[0], ~in_1[1], ~in_1[2], ~in_2, ~in_3);  // AND_Gate
  and and_2 (and_2_out, ~in_1[1], in_1[0], in_2, in_3);  // AND_Gate
  and and_3 (and_3_out, in_1[1], ~in_1[0], in_3, ~in_2);  // AND_Gate
  and and_4 (and_4_out, ~in_1[1], in_1[0], in_3, ~in_2);  // AND_Gate
  and and_5 (and_5_out, ~in_1[1], in_1[0], ~in_3, in_2);  // AND_Gate
  and and_6 (and_6_out, in_1[1], ~in_1[0], ~in_3, ~in_2);  // AND_Gate
  and and_7 (and_7_out, ~in_1[1], in_1[0], ~in_2, ~in_3);  // AND_Gate
  or or_1 (out_7, and_1_out, and_2_out, and_3_out);
  or or_2 (out_6, and_1_out, and_4_out, and_3_out);
  or or_3 (out_5, and_1_out, and_5_out, and_6_out);
  or or_4 (out_4, and_1_out, and_7_out, and_6_out);

  // Other names for the same wires on the sheet: addr0 = in_2; addr1 = in_3; Op[2:0] = in_1; sel0 = out_4;
  //   sel1 = out_5; sel2 = out_6; sel3 = out_7
endmodule

module Err (
  input  [2:0] in_1,
  input  in_2,
  output out_3
);

  wire comparator_1_eq, comparator_2_eq, comparator_3_eq, comparator_4_eq, comparator_5_eq, not_1_out,
       or_1_out;

  Comparator #(.width(3), .mode("unsigned")) comparator_1 (.a(in_1), .b(3'b000), .eq(comparator_1_eq));  // open: gt, lt
  Comparator #(.width(3), .mode("unsigned")) comparator_2 (.a(in_1), .b(3'b001), .eq(comparator_2_eq));  // open: gt, lt
  Comparator #(.width(3), .mode("unsigned")) comparator_3 (.a(in_1), .b(3'b010), .eq(comparator_3_eq));  // open: gt, lt
  Comparator #(.width(3), .mode("unsigned")) comparator_4 (.a(in_1), .b(3'b101), .eq(comparator_4_eq));  // open: gt, lt
  Comparator #(.width(3), .mode("unsigned")) comparator_5 (.a(in_1), .b(3'b110), .eq(comparator_5_eq));  // open: gt, lt
  or or_1 (or_1_out, comparator_1_eq, comparator_2_eq, comparator_3_eq, comparator_4_eq, comparator_5_eq);
  not not_1 (not_1_out, or_1_out);
  or or_2 (out_3, not_1_out, in_2);

  // Other names for the same wires on the sheet: r = out_3; t = in_2; tunnel[2:0] = in_1
endmodule
